// Logisim project CPUV2.circ as structural Verilog: 11 circuits, main circuit CPU
module CPU (
  input  [6:0] IN_1,
  input  EN_CLK,
  input  IN_2,
  input  STEP,
  input  CLR,
  input  [15:0] RAM_ADDRESS,
  input  [15:0] RAM_DATA,
  input  in_8,
  input  LD,
  input  EN,
  output CLR_OUT,
  output CLK_OUT,
  output KEYBOARD_RD,
  output [6:0] WR,
  output WR_2,
  output [15:0] pc,
  output [15:0] STACK,
  output [15:0] A,
  output [15:0] RAM_DATA_2,
  output [15:0] B,
  output [15:0] C,
  output [15:0] D,
  output [15:0] E,
  output OUT2,
  output [15:0] H,
  output [15:0] L
);

  wire and_1_out, and_2_out, and_3_out, and_4_out, and_5_out, and_6_out, and_7_out, and_8_out, and_9_out,
       and_10_out, and_11_out, and_12_out, and_13_out, and_14_out, c_t, clock_1_out, CY, CY_out, DCE, E_t,
       EnCY, EnJEP, EnJM, EnJNZ, EnJOP, EnJZ, EP, EP_out, INC, J_plus, JM, JM_out, JMP, JNZ, JNZ_out, JP,
       JUMP_out, JZ_out, L_t, l_t_t, nCY, NCY_out, not_1_out, not_2_out, not_3_out, not_4_out, not_5_out,
       not_6_out, not_7_out, not_8_out, O, OP_out, or_4_out, or_5_out, or_6_out, or_7_out, or_8_out,
       or_9_out, or_10_out, PC_Stack, r;
  wire [3:0] controll_unit_1_output1;
  wire [4:0] controll_unit_1_output1_3, controll_unit_1_output1_5;
  wire [5:0] ALU_out_17;
  wire [5:1] controll_unit_1_output1_4;
  wire [7:1] controll_unit_1_output2;
  wire [15:0] ALU_output, bit_extender_1_out, bit_extender_2_out, bit_extender_4_out,
       controlled_buffer_1_out, INSTRUCTION_REGISTER_output, MAR_output, or_2_out, or_3_out, ram_1_data,
       register_1_output, register_2_output, REGISTERS_data_out;
  wire [21:10] controll_unit_1_output1_2;
  wire [31:14] controll_unit_1_output2_2;

  not not_1 (not_1_out, controll_unit_1_output2_2[14]);
  Clock clock_1 (.out(clock_1_out));
  not not_2 (not_2_out, JM);
  and u_JP (JP, not_2_out, J_plus);
  and and_1 (and_1_out, not_1_out, EN_CLK, clock_1_out);
  or or_1 (CLK_OUT, and_1_out, STEP);
  and JZ (JZ_out, ALU_out_17[0], EnJZ);
  and u_JNZ (JNZ_out, JNZ, EnJNZ);
  and u_JM (JM_out, JM, EnJM);
  and u_CY (CY_out, CY, EnCY);
  and u_EP (EP_out, ALU_out_17[5], EnJEP);
  and OP (OP_out, EP, EnJOP);
  not not_3 (not_3_out, CY);
  and u_NCY (NCY_out, not_3_out, nCY);
  or JUMP (JUMP_out, JZ_out, CY_out, JNZ_out, JM_out, JP, EP_out, OP_out, JMP, NCY_out);
  assign or_2_out = MAR_output | RAM_ADDRESS;  // OR_Gate or_2, 16 bits wide
  assign or_3_out = RAM_DATA | controlled_buffer_1_out;  // OR_Gate or_3, 16 bits wide
  not not_4 (not_4_out, PC_Stack);
  and and_2 (and_2_out, not_4_out, JUMP_out);
  or or_4 (or_4_out, CLK_OUT, LD);
  or or_5 (or_5_out, LD, controll_unit_1_output1[1]);
  and and_3 (and_3_out, PC_Stack, EnJNZ, not_5_out);
  not not_5 (not_5_out, JNZ);
  and and_4 (and_4_out, PC_Stack, EnJZ, JNZ);
  and and_5 (and_5_out, PC_Stack, EnJM, not_6_out);
  not not_6 (not_6_out, JM);
  and and_6 (and_6_out, PC_Stack, J_plus, JM);
  and and_7 (and_7_out, PC_Stack, EnCY, not_7_out);
  not not_7 (not_7_out, CY);
  and and_8 (and_8_out, PC_Stack, nCY, CY);
  and and_9 (and_9_out, PC_Stack, EnJEP, EP);
  and and_10 (and_10_out, PC_Stack, EnJOP, not_8_out);
  not not_8 (not_8_out, EP);
  assign bit_extender_1_out = {{9{1'b0}}, IN_1};  // Bit_Extender bit_extender_1
  assign bit_extender_2_out = {{15{1'b0}}, IN_2};  // Bit_Extender bit_extender_2
  assign controlled_buffer_1_out = controll_unit_1_output2[2] ? bit_extender_2_out : 16'bz;  // Controlled_Buffer controlled_buffer_1
  assign controlled_buffer_1_out = controll_unit_1_output2[6] ? pc : 16'bz;  // Controlled_Buffer controlled_buffer_2
  Counter #(.width(16), .max('hffff)) counter_1 (
    .load(and_2_out), .D(controlled_buffer_1_out), .count(controll_unit_1_output2[3]), .Q(pc), .clk(CLK_OUT),
    .clr(CLR));  // open: carry
  Counter #(.width(16), .max('hffff)) counter_2 (
    .load(controll_unit_1_output2[4]), .D(controlled_buffer_1_out), .count(controll_unit_1_output2[5]),
    .Q(STACK), .clk(CLK_OUT), .clr(CLR));  // open: carry
  assign controlled_buffer_1_out = controll_unit_1_output2[7] ? STACK : 16'bz;  // Controlled_Buffer controlled_buffer_3
  Register MAR (
    .INPUT(controlled_buffer_1_out), .CLK(CLK_OUT), .CLR(CLR), .OUTPUT(MAR_output), .SHL(1'b0), .SHR(1'b0),
    .INC(controll_unit_1_output2_2[15]), .LD(controll_unit_1_output1[0]), .DEC(1'b0), .EN(1'b1));  // open: out_11
  RAM #(.addrWidth(16), .dataWidth(16), .bus("separate")) ram_1 (
    .addr(or_2_out), .din(or_3_out), .data(ram_1_data), .str(or_5_out), .clk(or_4_out), .ld(or_6_out),
    .clr(in_8));  // open: sel
  Demultiplexer #(.width(16), .enable("false")) demultiplexer_1 (
    .out0(controlled_buffer_1_out), .out1(RAM_DATA_2), .in(ram_1_data), .sel(EN));
  or or_6 (or_6_out, controll_unit_1_output1[2], EN);
  Register INSTRUCTION_REGISTER (
    .INPUT(controlled_buffer_1_out), .CLK(CLK_OUT), .CLR(CLR), .OUTPUT(INSTRUCTION_REGISTER_output),
    .SHL(1'b0), .SHR(1'b0), .INC(1'b0), .LD(controll_unit_1_output1[3]), .DEC(1'b0), .EN(1'b1));  // open: out_11
  or or_7 (or_7_out, CLR, or_8_out);
  assign controlled_buffer_1_out = controll_unit_1_output2[1] ? bit_extender_1_out : 16'bz;  // Controlled_Buffer controlled_buffer_4
  or or_8 (or_8_out, and_3_out, and_4_out, and_5_out, and_6_out, and_7_out, and_8_out, and_9_out, and_10_out);
  assign controlled_buffer_1_out = controll_unit_1_output2_2[16] ? ALU_output : 16'bz;  // Controlled_Buffer controlled_buffer_5
  Controll_Unit controll_unit_1 (
    .\input (INSTRUCTION_REGISTER_output), .CLR(or_7_out),
    .output1({controll_unit_1_output1, controll_unit_1_output1_4, WR_2, controll_unit_1_output1_2, controll_unit_1_output1_5, controll_unit_1_output1_3}),
    .output2({controll_unit_1_output2_2[31], OUT2, PC_Stack, J_plus, nCY, JMP, INC, DCE, c_t, l_t_t, r, E_t, L_t, controll_unit_1_output2_2[18:14], EnJOP, EnJEP, EnCY, EnJM, EnJNZ, EnJZ, controll_unit_1_output2, KEYBOARD_RD}),
    .CLK(CLK_OUT));
  Bit_Extender #(.in_width(16), .out_width(7)) bit_extender_3 (.in(controlled_buffer_1_out), .out(WR));
  assign controlled_buffer_1_out = controll_unit_1_output1_4[1] ? register_1_output : 16'bz;  // Controlled_Buffer controlled_buffer_6
  TTY tty_1 (.data(WR), .clk(CLK_OUT), .we(WR_2), .clr(CLR));
  Register register_1 (
    .INPUT(controlled_buffer_1_out), .CLK(CLK_OUT), .CLR(CLR), .OUTPUT(register_1_output),
    .SHL(controll_unit_1_output1_3[4]), .SHR(controll_unit_1_output1_3[3]),
    .INC(controll_unit_1_output1_3[1]), .LD(controll_unit_1_output1_3[2]),
    .DEC(controll_unit_1_output1_3[0]), .EN(1'b1));  // open: out_11
  Regiaters REGISTERS (
    .DATA_IN(controlled_buffer_1_out), .SEL_IN(controll_unit_1_output1_2[17:14]), .CLK(CLK_OUT), .CLR(CLR),
    .shl(controll_unit_1_output1_5[4]), .shr(controll_unit_1_output1_5[3]),
    .LD(controll_unit_1_output1_5[2]), .inc(or_10_out), .dec(or_9_out), .DATA_OUT_2(controlled_buffer_1_out),
    .SEL_OUT(controll_unit_1_output1_2[13:10]), .EN(controll_unit_1_output1_4[5]),
    .DATA_OUT(REGISTERS_data_out), .OVERFLOW(O), .a(A), .b(B), .c(C), .d(D), .e(E), .h(H), .l(L));
  ALU ALU (
    .A(REGISTERS_data_out), .OUTPUT(ALU_output), .B(register_1_output),
    .sel(controll_unit_1_output1_2[21:18]), .J(controll_unit_1_output1_4[3]), .CLK(CLK_OUT),
    .K(controll_unit_1_output1_4[4]), .CLR(CLR), .CY(CY), .out_17(ALU_out_17[0]), .out_18(JM), .ODD(EP),
    .EVEN(ALU_out_17[5]), .in_4(E_t), .in_6(c_t), .in_5(r), .in_7(l_t_t), .in_8(L_t));  // open: remainder, out_15, out_19
  and and_11 (and_11_out, controll_unit_1_output2_2[18], CY);
  and and_12 (and_12_out, CY, controll_unit_1_output2_2[17]);
  or or_9 (or_9_out, and_11_out, and_14_out, controll_unit_1_output1_5[0]);
  or or_10 (or_10_out, and_12_out, and_13_out, controll_unit_1_output1_5[1]);
  not not_9 (JNZ, ALU_out_17[0]);
  and and_13 (and_13_out, O, INC);
  assign bit_extender_4_out = {{10{1'b0}}, {ALU_out_17[5], EP, CY, JM, JNZ, ALU_out_17[0]}};  // Bit_Extender bit_extender_4
  and and_14 (and_14_out, O, DCE);
  assign controlled_buffer_1_out = controll_unit_1_output1_4[2] ? register_2_output : 16'bz;  // Controlled_Buffer controlled_buffer_7
  Register register_2 (
    .INPUT(bit_extender_4_out), .CLK(CLK_OUT), .CLR(CLR), .OUTPUT(register_2_output), .SHL(1'b0), .SHR(1'b0),
    .INC(1'b0), .LD(1'b1), .DEC(1'b0), .EN(1'b1));  // open: out_11

  assign CLR_OUT = CLR;

  // Notes on the sheet:
  //   Key Board/INPUT 1
  //   RAM
  //   INPUT  2
  //   PROGRAM POINTER
  //   STACK POINTER
  //   Controll-Unit
  //   TMP register
  //   Output 1
  //   06 - MOV A,A 
  //   08 - MOV A,B
  //   0a - MOV A,C
  //   0c - MOV A,D
  //   0e - MOV A,E
  //   10 - MOV A,H
  //   12 - MOV A,L
  //   28 - MOV C,A
  //   2a - MOV C,B
  //   2c - MOV C,C
  //   2e - MOV C,D
  //   30 - MOV C,E
  //   32 - MOV C,L
  //   34 - MOV C,H
  //   36 - MOV C,M(L REG)
  //   4a - MOV E,A
  //   4c - MOV E,B
  //   4e - MOV E,C
  //   50 - MOV E,D
  //   52 - MOV E,E
  //   54 - MOV E,L
  //   56 - MOV E,H
  //   58 - MOV E,M(L REG)
  //   14 - MOV A, M(L REG)
  //   6c - MOV H,A
  //   6e - MOV H,B
  //   70 - MOV H,C
  //   72 - MOV H,D
  //   74 - MOV H,E
  //   76 - MOV H,L
  //   78 - MOV H,H 
  //   7a - MOV H,M(L REG)
  //   92 - MVI A,dd
  //   95 - MVi B,dd
  //   98 - MVi C,dd
  //   9b - MVI D,dd
  //   9e - MVI E,dd
  //   a1 - MVI Hdd
  //   a4 - MVI L,dd
  //   03 - NOP
  //   05 -HULT
  //   da - STC
  //   dc - CMC
  //   de - ADD A
  //   e1 - ADD B
  //   e4 - ADD C
  //   e7 - ADD D
  //   ea - ADD E
  //   ed - ADD H
  //   f0 - ADD L
  //   f3 - ADD M(L REG)
  //   118 - SUB A
  //   11b - SUB B
  //   11e - SUB C
  //   121 - SUB D
  //   124 - SUB E
  //   127 - SUB H
  //   12a - SUB L
  //   12d - SUB M(L REG)
  //   152 - DAD B
  //   159 - DAD D
  //   160 - DAD H
  //   167 - ADI dd
  //   16b - ACI dd
  //   170 - SUI dd
  //   174 - SBI dd
  //   179 - DAA 
  //   194 - XRA A
  //   197 - XRA B
  //   19a - XRA C
  //   19d - XRA D
  //   1a0 - XRA E
  //   1a3 - XRA H
  //   1a6 - XRA L
  //   1a9 - XRA M(L REG)
  //   a7 - LXI B,dddd
  //   ac - LXI D,dddd
  //   b1 - LXI H,dddd
  //   b6 - LDAX B
  //   b9 - LDAX D
  //   bc - LHLD aaaa
  //   c3 - LDA  aa
  //   c6 - STA aa
  //   cb - ATAX B
  //   c7 - ATAX D
  //   ce - SHLD aaaa
  //   d3 - XCHG
  //   f7 - ADC A
  //   fb - ADC B
  //   ff - ADC C
  //   103 - ADC D
  //   107 - ADC E
  //   10b - ADC H
  //   10f - ADC L
  //   113 - ADC M(L REG)
  //   131 - SBB A
  //   135 -  SBB B
  //   139 - SBB C
  //   13d - SBB D
  //   141 -  SBB E
  //   145 - SBB H
  //   149 - SBB L
  //   14d - SBB M(L REG)
  //   17b - AND A
  //   17e - AND B
  //   181 - AND C
  //   184 - AND D
  //   187 - AND E
  //   18a - AND H
  //   18d - AND L
  //   190 - AND M(L REG)
  //   1ad - ORA A
  //   1b0 - ORA B
  //   1b3 - ORA C
  //   1b6 - ORA D
  //   1b9 - ORA E
  //   1bc - ORA H
  //   1bf - ORA L
  //   1c2 - ORA M(L REG)
  //   1c6 - ANI dd
  //   1ca - XRI dd
  //   1ce - ORI dd
  //   1d2 - CMA
  //   17 - MOV B,A
  //   19 - MOV B,B
  //   1b - MOV B,C
  //   1d - MOV B,D
  //   1f - MOV B,E
  //   21 - MOV B,L
  //   23 - MOV B,H 
  //   25 - MOV B, M(L REG)
  //   39 - MOV D,A
  //   3b - MOV D,B
  //   3d - MOV D,C
  //   3f - MOV D,D
  //   41 - MOV D,E
  //   43 - MOV D,L
  //   45 - MOV D,H
  //   47 - MOV C, M(L REG)
  //   5b -MOV L,A
  //   5d - MOV L,B
  //   5f - MOV L,C
  //   61 - MOV L,D
  //   63 - MOV L,E
  //   65 - MOV L,H
  //   67 - MOV L,L
  //   69 - MOV L,M (L REG) 
  //   7d - MOV - M(L REG), A
  //   80 - MOV - M(L REG), B
  //   83 - MOV -M,(L REG),C
  //   86 - MOV - M,(L REG), D
  //   89 - MOV - M,(L REG) E
  //   8c - MOV - M(L REG), L
  //   8f - MOV - M(L REG),H
  //   297 - RZ
  //   29b - RC
  //   2ab - RP
  //   2af - RM
  //   1d4 - RLC
  //   1d8 - RRC
  //   1dc - RAR
  //   1de - RAL
  //   1e0 - INR A
  //   1e2 - INR B
  //   1e4 - INR C
  //   1e6 - INR D
  //   1e8 - INR E
  //   1ea - INR H
  //   1ec - INR L
  //   1fc - INR M(L REG)
  //   1ee - DCR A
  //   1f0 - DCR B
  //   1f2 - DCR C
  //   1f4 - DCR D
  //   1f6 - DCR E
  //   1f8- DCR H
  //   1fa - DCR L
  //   201 - DCR M(L REG)
  //   206 - INX B
  //   209 - INX D
  //   20c - INX H
  //   20f - DCX B
  //   212  - DCX D
  //   215 - DCX H
  //   218 - JMP aaaa
  //   21a - PCHL
  //   21d - CMP A
  //   220 - CMP B
  //   223 - CMP C
  //   226 - CMP D
  //   229 - CMP E
  //   22c - CMP H
  //   22f - CMP L
  //   232 - CMP M(L REG)
  //   236 - CPI dd
  //   23d - JNZ aaaa
  //   23a - JZ aaaa
  //   240 - JNC aaaa
  //   243 - JC aaaa
  //   246 - JPO aaaa
  //   249 - JPE aaaa
  //   24c - JP aaaa
  //   24f - JM aaaa
  //   252 - CALL aaaa
  //   258 - CNZ aaaa
  //   25f - CZ aaaa
  //   266 - CC aaaa
  //   26d - CNC aaaa
  //   274 - CPE aaaa
  //   27b - CPO aaaa
  //   282 - CP aaaa
  //   281 - CM aaaa
  //   290 - RET
  //   293 - RNZ
  //   29f - RNC
  //   2a3 - RPE
  //   2a7 - RPO
  //   2b3 - LXI SP,dddd
  //   2b6 - DAD SP
  //   2b9 - INX SP
  //   2bb - DCX SP
  //   2bd - PUSH B
  //   2c4 - PUSH D
  //   2cb - PUSH H
  //   2d3 - PUSH PSW
  //   2da - POP B
  //   2df - POP D
  //   2e4 - POP H
  //   2e9 - POP PSW
  //   2ee - XTHL
  //   2f7 - SPHL
  //   2f9 - IN 1
  //   2fb - IN 2
  //   2fd - OUT 1
  //   2ff - OUT 2
endmodule

module Register (
  input  [15:0] INPUT,
  input  CLK,
  input  CLR,
  input  EN,
  input  SHL,
  input  SHR,
  input  INC,
  input  LD,
  input  DEC,
  output [15:0] OUTPUT,
  output out_11
);

  wire and_5_out, and_6_out, and_7_out, or_1_out, or_2_out;
  wire [0:0] and_2_out, and_3_out;
  wire [15:0] and_1_out, and_4_out, not_1_out, or_3_out, shifter_1_out, shifter_2_out;

  assign and_1_out = INPUT & {16{LD}};  // AND_Gate and_1, 16 bits wide
  Shifter #(.width(16), .shift("rl")) shifter_1 (.in(OUTPUT), .\dist ({3'b000, and_2_out[0]}), .out(shifter_1_out));
  and and_2 (and_2_out[0], SHL, EN);
  Shifter #(.width(16), .shift("rr")) shifter_2 (
    .in(shifter_1_out), .\dist ({3'b000, and_3_out[0]}), .out(shifter_2_out));
  and and_3 (and_3_out[0], SHR, EN);
  assign and_4_out = not_1_out & shifter_2_out;  // AND_Gate and_4, 16 bits wide
  assign not_1_out = ~{16{LD}};  // NOT_Gate not_1, 16 bits wide
  or or_1 (or_1_out, and_2_out[0], and_7_out, and_5_out, and_3_out[0]);
  or or_2 (or_2_out, and_7_out, and_6_out);
  assign or_3_out = and_4_out | and_1_out;  // OR_Gate or_3, 16 bits wide
  Counter #(.width(16), .max('hffff)) counter_1 (
    .load(or_1_out), .D(or_3_out), .count(or_2_out), .Q(OUTPUT), .carry(out_11), .clk(CLK), .clr(CLR));
  and and_5 (and_5_out, EN, LD);
  and and_6 (and_6_out, INC, EN);
  and and_7 (and_7_out, EN, DEC);
endmodule

module Regiaters (
  input  [15:0] DATA_IN,
  input  [3:0] SEL_IN,
  input  CLK,
  input  CLR,
  input  shl,
  input  shr,
  input  LD,
  input  inc,
  input  dec,
  input  [3:0] SEL_OUT,
  input  EN,
  output [15:0] a,
  output [15:0] b,
  output [15:0] c,
  output [15:0] d,
  output [15:0] e,
  output [15:0] h,
  output [15:0] l,
  output [15:0] DATA_OUT,
  output OVERFLOW,
  output [15:0] DATA_OUT_2
);

  wire A_t, B_t, C_t, D_t, demultiplexer_2_out0, demultiplexer_2_out1, demultiplexer_2_out2,
       demultiplexer_2_out3, demultiplexer_2_out4, demultiplexer_2_out5, demultiplexer_2_out6, E_t, F, L_t;
  wire [15:0] demultiplexer_1_out0, demultiplexer_1_out1, demultiplexer_1_out2, demultiplexer_1_out3,
       demultiplexer_1_out4, demultiplexer_1_out5, demultiplexer_1_out6;

  Demultiplexer #(.select(4), .width(16), .enable("false")) demultiplexer_1 (
    .out0(demultiplexer_1_out0), .out1(demultiplexer_1_out1), .out2(demultiplexer_1_out2),
    .out3(demultiplexer_1_out3), .out4(demultiplexer_1_out4), .out5(demultiplexer_1_out5),
    .out6(demultiplexer_1_out6), .in(DATA_IN), .sel(SEL_IN));  // open: out7, out8, out9, out10, out11, out12, out13, out14, out15
  Demultiplexer #(.select(4), .enable("false")) demultiplexer_2 (
    .out0(demultiplexer_2_out0), .out1(demultiplexer_2_out1), .out2(demultiplexer_2_out2),
    .out3(demultiplexer_2_out3), .out4(demultiplexer_2_out4), .out5(demultiplexer_2_out5),
    .out6(demultiplexer_2_out6), .in(1'b1), .sel(SEL_IN));  // open: out7, out8, out9, out10, out11, out12, out13, out14, out15
  Register u_A (
    .INPUT(demultiplexer_1_out0), .CLK(CLK), .CLR(CLR), .OUTPUT(a), .SHL(shl), .SHR(shr), .INC(inc), .LD(LD),
    .DEC(dec), .EN(demultiplexer_2_out0), .out_11(A_t));
  Register u_B (
    .INPUT(demultiplexer_1_out1), .CLK(CLK), .CLR(CLR), .OUTPUT(b), .SHL(shl), .SHR(shr), .INC(inc), .LD(LD),
    .DEC(dec), .EN(demultiplexer_2_out1), .out_11(B_t));
  Register u_C (
    .INPUT(demultiplexer_1_out2), .CLK(CLK), .CLR(CLR), .OUTPUT(c), .SHL(shl), .SHR(shr), .INC(inc), .LD(LD),
    .DEC(dec), .EN(demultiplexer_2_out2), .out_11(C_t));
  Register u_D (
    .INPUT(demultiplexer_1_out3), .CLK(CLK), .CLR(CLR), .OUTPUT(d), .SHL(shl), .SHR(shr), .INC(inc), .LD(LD),
    .DEC(dec), .EN(demultiplexer_2_out3), .out_11(D_t));
  Register u_E (
    .INPUT(demultiplexer_1_out4), .CLK(CLK), .CLR(CLR), .OUTPUT(e), .SHL(shl), .SHR(shr), .INC(inc), .LD(LD),
    .DEC(dec), .EN(demultiplexer_2_out4), .out_11(E_t));
  Register u_H (
    .INPUT(demultiplexer_1_out5), .CLK(CLK), .CLR(CLR), .OUTPUT(h), .SHL(shl), .SHR(shr), .INC(inc), .LD(LD),
    .DEC(dec), .EN(demultiplexer_2_out5), .out_11(F));
  Register u_L (
    .INPUT(demultiplexer_1_out6), .CLK(CLK), .CLR(CLR), .OUTPUT(l), .SHL(shl), .SHR(shr), .INC(inc), .LD(LD),
    .DEC(dec), .EN(demultiplexer_2_out6), .out_11(L_t));
  Multiplexer #(.select(4), .width(16), .enable("false")) multiplexer_1 (
    .in0(a), .in1(b), .in2(c), .in3(d), .in4(e), .in5(h), .in6(l), .out(DATA_OUT), .sel(SEL_OUT));  // open: in7, in8, in9, in10, in11, in12, in13, in14, in15
  assign DATA_OUT_2 = EN ? DATA_OUT : 16'bz;  // Controlled_Buffer controlled_buffer_1
  Multiplexer #(.select(4), .enable("false")) multiplexer_2 (
    .in0(A_t), .in1(B_t), .in2(C_t), .in3(D_t), .in4(E_t), .in5(F), .in6(L_t), .out(OVERFLOW), .sel(SEL_OUT));  // open: in7, in8, in9, in10, in11, in12, in13, in14, in15
endmodule

// JM
module ALU (
  input  [15:0] A,
  input  [15:0] B,
  input  [3:0] sel,
  input  in_4,
  input  in_5,
  input  in_6,
  input  in_7,
  input  in_8,
  input  J,
  input  CLK,
  input  K,
  input  CLR,
  output [15:0] remainder,
  output CY,
  output out_15,
  output [15:0] OUTPUT,
  output out_17,
  output out_18,
  output out_19,
  output ODD,
  output EVEN
);

  wire adder_1_cout, and_2_out, and_3_out, and_4_out, and_5_out, and_6_out, and_8_out, and_9_out,
       comparator_1_eq, comparator_2_gt, comparator_3_eq, comparator_4_eq, comparator_5_eq, J_t, K_t,
       not_3_out, or_2_out, or_3_out, subtractor_1_bout;
  wire [4:0] bit_extender_3_out, bitadder_1_out;
  wire [15:0] adder_1_out, and_1_out, bcd_1_out_2, bit_extender_1_out, bit_extender_2_out, divider_1_out,
       multiplier_1_cout, multiplier_1_out, nand_1_out, nor_1_out, not_1_out, or_1_out, subtractor_1_out,
       xnor_1_out, xor_1_out;
  wire [16:0] out;

  assign and_1_out = A & B;  // AND_Gate and_1, 16 bits wide
  assign or_1_out = A | B;  // OR_Gate or_1, 16 bits wide
  assign nand_1_out = ~(A & B);  // NAND_Gate nand_1, 16 bits wide
  assign nor_1_out = ~(A | B);  // NOR_Gate nor_1, 16 bits wide
  assign xor_1_out = A ^ B;  // XOR_Gate xor_1, 16 bits wide
  assign xnor_1_out = ~(A ^ B);  // XNOR_Gate xnor_1, 16 bits wide
  Adder #(.width(16)) adder_1 (.a(A), .b(B), .out(adder_1_out), .cout(adder_1_cout));  // open: cin
  Subtractor #(.width(16)) subtractor_1 (.a(A), .b(B), .out(subtractor_1_out), .bout(subtractor_1_bout));  // open: bin
  Multiplier #(.width(16)) multiplier_1 (.a(A), .b(B), .out(multiplier_1_out), .cout(multiplier_1_cout));  // open: cin
  Divider #(.width(16)) divider_1 (.a(A), .b(B), .out(divider_1_out), .rem(remainder));  // open: upper
  assign bit_extender_1_out = {{15{1'b0}}, comparator_1_eq};  // Bit_Extender bit_extender_1
  Comparator #(.width(16)) comparator_1 (.a(A), .b(B), .eq(comparator_1_eq));  // open: gt, lt
  BitAdder #(.width(16)) bitadder_1 (.in0(A), .out(bitadder_1_out));
  BCD bcd_1 (.in_1(A), .out_2(bcd_1_out_2));
  assign not_1_out = ~A;  // NOT_Gate not_1, 16 bits wide
  assign bit_extender_2_out = {{11{1'b0}}, bitadder_1_out};  // Bit_Extender bit_extender_2
  Multiplexer #(.select(4), .width(16), .enable("false")) multiplexer_1 (
    .in0(and_1_out), .in1(nand_1_out), .in2(or_1_out), .in3(nor_1_out), .in4(xor_1_out), .in5(xnor_1_out),
    .in6(adder_1_out), .in7(subtractor_1_out), .in8(multiplier_1_out), .in9(divider_1_out),
    .in10(bit_extender_1_out), .in11(out[15:0]), .in13(not_1_out), .in14(bit_extender_2_out),
    .in15(bcd_1_out_2), .out(OUTPUT), .sel(sel));  // open: in12
  Comparator #(.width(16)) comparator_2 (.a(multiplier_1_cout), .b({16{1'b0}}), .gt(comparator_2_gt));  // open: eq, lt
  Comparator #(.width(4)) comparator_3 (.a(sel), .b(4'b0110), .eq(comparator_3_eq));  // open: gt, lt
  Comparator #(.width(4)) comparator_4 (.a(sel), .b(4'b0111), .eq(comparator_4_eq));  // open: gt, lt
  Comparator #(.width(5)) comparator_5 (.a(bit_extender_3_out), .b(5'b01000), .eq(comparator_5_eq));  // open: gt, lt
  assign bit_extender_3_out = {{1{1'b0}}, sel};  // Bit_Extender bit_extender_3
  and and_2 (and_2_out, adder_1_cout, comparator_3_eq);
  and and_3 (and_3_out, subtractor_1_bout, comparator_4_eq);
  and and_4 (and_4_out, comparator_2_gt, comparator_5_eq);
  Comparator #(.width(16)) comparator_6 (.a(A), .b({16{1'b0}}), .gt(out_15), .eq(out_17), .lt(out_18));
  or or_2 (or_2_out, CY, and_4_out, and_2_out, and_3_out, J_t, J);
  or or_3 (or_3_out, K, K_t);
  J_K_Flip_Flop j_k_ff_1 (.J(or_2_out), .clk(CLK), .K(or_3_out), .Q(CY), .reset(CLR));  // open: Qn, preset, en
  xor odd_parity_1 (ODD, A[0], A[1], A[2], A[3], A[4], A[5], A[6], A[7], A[8], A[9], A[10], A[11], A[12], A[13], A[14], A[15]);
  not not_2 (EVEN, ODD);
  RAL ral_1 (.in_5(in_6), .in_3(in_4), .out_8(out), .in_2({CY, A}), .in_4(CLK), .in_1(in_8), .in_7(in_7), .in_6(in_5));
  and and_5 (and_5_out, in_4, and_6_out);
  and and_6 (and_6_out, out[15], in_7);
  and and_7 (K_t, in_4, not_3_out);
  not not_3 (not_3_out, J_t);
  or or_4 (J_t, and_5_out, and_8_out);
  and and_8 (and_8_out, in_4, and_9_out);
  and and_9 (and_9_out, in_5, out[0]);

  assign out_19 = A[15];

  // Other names for the same wires on the sheet: AOUT[16:0] = {CY, A}; clk2 = in_4; l = in_7; out2[15:0] = out[15:0];
  //   R = in_5
endmodule

module FloatingPointRegister (
  input  in_1,
  input  in_2,
  input  in_3,
  input  [31:0] in_4
);

  wire and_1_out, and_2_out, not_2_out, or_1_out, sign_q;
  wire [7:0] and_3_out, and_4_out, exponent_q, or_2_out;
  wire [7:7] not_1_out;
  wire [22:0] and_5_out, and_6_out, mantissa_q, or_3_out;

  not not_1 (not_1_out[7], in_1);
  and and_1 (and_1_out, in_4[31], in_1);
  and and_2 (and_2_out, not_1_out[7], sign_q);
  or or_1 (or_1_out, and_1_out, and_2_out);
  not not_2 (not_2_out, or_1_out);
  J_K_Flip_Flop sign (.J(or_1_out), .clk(in_2), .K(not_2_out), .Q(sign_q), .reset(in_3));  // open: Qn, preset, en
  Register_part exponent (.D(or_2_out), .Q(exponent_q), .clk(in_2), .clr(in_3));  // open: en
  assign and_3_out = {8{in_1}} & in_4[30:23];  // AND_Gate and_3, 8 bits wide
  assign and_4_out = {8{not_1_out[7]}} & exponent_q;  // AND_Gate and_4, 8 bits wide
  assign or_2_out = and_3_out | and_4_out;  // OR_Gate or_2, 8 bits wide
  assign and_5_out = {23{not_1_out[7]}} & mantissa_q;  // AND_Gate and_5, 23 bits wide
  assign and_6_out = in_4[22:0] & {23{in_1}};  // AND_Gate and_6, 23 bits wide
  assign or_3_out = and_6_out | and_5_out;  // OR_Gate or_3, 23 bits wide
  Register_part #(.width(23)) mantissa (.D(or_3_out), .Q(mantissa_q), .clk(in_2), .clr(in_3));  // open: en
endmodule

module Controll_Unit (
  input  [15:0] \input ,
  input  CLR,
  input  CLK,
  output [31:0] output1,
  output [31:0] output2
);

  wire and_1_out, comparator_1_eq, comparator_1_gt, comparator_2_eq, comparator_2_gt, or_1_out, or_2_out,
       or_3_out;
  wire [4:0] counter_1_q;
  wire [15:0] adder_1_out, adder_2_out, bit_extender_1_out, controlled_buffer_1_out, multiplexer_1_out,
       subtractor_1_out;

  assign bit_extender_1_out = {{11{1'b0}}, counter_1_q};  // Bit_Extender bit_extender_1
  Comparator #(.width(16)) comparator_1 (
    .a(bit_extender_1_out), .b(16'h2), .gt(comparator_1_gt), .eq(comparator_1_eq));  // open: lt
  Adder #(.width(16)) adder_1 (.a(\input ), .b(16'h1), .out(adder_1_out));  // open: cin, cout
  Adder #(.width(16)) adder_2 (.a(\input ), .b(subtractor_1_out), .out(adder_2_out));  // open: cin, cout
  or or_1 (or_1_out, comparator_1_gt, comparator_1_eq);
  Subtractor #(.width(16)) subtractor_1 (.a(bit_extender_1_out), .b(16'h2), .out(subtractor_1_out));  // open: bin, bout
  assign controlled_buffer_1_out = or_1_out ? adder_2_out : 16'bz;  // Controlled_Buffer controlled_buffer_1
  Counter #(.width(5), .max('h1f), .trigger("falling")) counter_1 (
    .count(1'b1), .Q(counter_1_q), .clk(CLK), .clr(or_3_out));  // open: load, D, carry
  or or_2 (or_2_out, comparator_2_gt, comparator_2_eq);
  Comparator #(.width(16)) comparator_2 (
    .a(controlled_buffer_1_out), .b(adder_1_out), .gt(comparator_2_gt), .eq(comparator_2_eq));  // open: lt
  Multiplexer #(.select(5), .width(16)) multiplexer_1 (
    .in0({16{1'b0}}), .in1(16'h1), .in2(controlled_buffer_1_out), .in3(controlled_buffer_1_out),
    .in4(controlled_buffer_1_out), .in5(controlled_buffer_1_out), .in6(controlled_buffer_1_out),
    .in7(controlled_buffer_1_out), .in8(controlled_buffer_1_out), .in9(controlled_buffer_1_out),
    .in10(controlled_buffer_1_out), .in11(controlled_buffer_1_out), .in12(controlled_buffer_1_out),
    .in13(controlled_buffer_1_out), .in14(controlled_buffer_1_out), .in15(controlled_buffer_1_out),
    .in16(controlled_buffer_1_out), .in17(controlled_buffer_1_out), .in18(controlled_buffer_1_out),
    .in19(controlled_buffer_1_out), .in20(controlled_buffer_1_out), .in21(controlled_buffer_1_out),
    .in22(controlled_buffer_1_out), .in23(controlled_buffer_1_out), .in24(controlled_buffer_1_out),
    .in25(controlled_buffer_1_out), .in26(controlled_buffer_1_out), .in27(controlled_buffer_1_out),
    .in28(controlled_buffer_1_out), .in29(controlled_buffer_1_out), .in30(controlled_buffer_1_out),
    .in31(controlled_buffer_1_out), .out(multiplexer_1_out), .sel(counter_1_q), .en(1'b1));
  and and_1 (and_1_out, output2[31], or_2_out);
  or or_3 (or_3_out, CLR, and_1_out);
  ROM #(.addrWidth(16), .dataWidth(32)) rom_1 (.addr(multiplexer_1_out), .data(output1), .sel(1'b1));
  ROM #(.addrWidth(16), .dataWidth(32)) rom_2 (.addr(multiplexer_1_out), .data(output2), .sel(1'b1));

  // Notes on the sheet:
  //   contents of rom_1 (hex, n*v repeats v):
  //   10000000 c0000000 4*0 8000040 0 8000480 0 8000880 0 8000c80 0 8001080 0 8001480 0 8001880 0 18001800
  //   40000080 0 8004080 0 8004480 0 8004880 0 8004c80 0 8005080 0 8005880 0 8005480 0 18001800 40004080 0
  //   8008080 0 8008480 0 8008880 0 8008c80 0 8009080 0 8009880 0 8009480 0 18001800 40008080 0 800c080 0
  //   800c480 0 800c880 0 800cc80 0 800d080 0 800d880 0 800d480 0 18001800 4000c080 0 8010080 0 8010480 0
  //   8010880 0 8010c80 0 8011080 0 8011880 0 8011480 0 18001800 40010080 0 8014080 0 8014480 0 8014880 0
  //   8014c80 0 8015080 0 8015880 0 8015480 0 18001800 40014080 0 8018080 0 8018480 0 8018880 0 8018c80 0
  //   8019080 0 8019480 0 8019880 0 18001800 40018080 0 18001800 28000080 0 18001800 28000400 0 18001800
  //   28008000 0 18001800 28000c00 0 18001800 28001000 0 18001800 28001400 0 18001800 28001800 0 10000000
  //   40000080 0 10000000 40004080 0 10000000 40008080 0 10000000 4000c080 0 10000000 40010080 0 10000000
  //   40014080 0 10000000 40018080 0 10000000 40004080 10000000 40008080 0 10000000 4000c080 10000000
  //   40010080 0 10000000 40014080 10000000 40018080 0 18000400 40000080 0 18000c00 40000080 0 10000000
  //   50000000 40014080 10000000 50000000 40018080 0 10000000 50000000 40000080 0 10000000 50000000
  //   28000000 0 18000400 28000000 0 10000000 50000000 28001400 28001800 0 8001404 8014c80 80c080 8001804
  //   8019080 810080 0 2000000 0 6000000 0 8000004 180080 0 8000404 180080 0 8000804 180080 0 8000c04
  //   180080 0 8001004 180080 0 8001404 180080 0 8001804 180080 0 18001800 40000004 180080 0 8000004
  //   180080 0 0 8000404 180080 0 0 8000804 180080 0 0 8000c04 180080 0 0 8001004 180080 0 0 8001404
  //   180080 0 0 8001804 180080 0 0 18001800 40000004 180080 0 0 8000004 1c0080 0 8000404 1c0080 0 8000804
  //   1c0080 0 8000c04 1c0080 0 8001004 1c0080 0 8001404 1c0080 0 8001804 1c0080 0 18001800 40000004
  //   1c0080 0 8000004 1c0080 0 0 8000404 1c0080 0 0 8000804 1c0080 0 0 8000c04 1c0080 0 0 8001004 1c0080
  //   0 0 8001404 1c0080 0 0 8001804 1c0080 0 0 18001800 40000004 1c0080 0 0 8001804 198880 14000 8001404
  //   194480 0 0 8001804 199080 c000 8001404 194c80 0 0 8001804 199880 14000 8001404 195480 14000 0
  //   10000000 40000004 180080 0 10000000 40000004 180080 0 0 10000000 40000004 1c0080 0 10000000 40000004
  //   1c0080 0 0 3c0080 0 8000004 80 0 8000404 80 0 8000804 80 0 8000c04 80 0 8001004 80 0 8001404 80 0
  //   8001804 80 0 18001800 40000004 80 0 8000004 100080 0 8000404 100080 0 8000804 100080 0 8000c04
  //   100080 0 8001004 100080 0 8001404 100080 0 8001804 100080 0 18001800 40000004 100080 0 8000004 80080
  //   0 8000404 80080 0 8000804 80080 0 8000c04 80080 0 8001004 80080 0 8001404 80080 0 8001804 80080 0
  //   18001800 40000004 80080 0 10000000 40000004 80 0 10000000 40000004 100080 0 10000000 40000004 80080
  //   0 340080 0 0 2c0000 2c0080 0 0 2c0000 2c0080 0 100 0 200 0 40 0 4040 0 8040 0 c040 0 10040 0 14040 0
  //   18040 0 20 0 4020 0 8020 0 c020 0 10020 0 14020 0 18020 0 18001800 40000004 2 20800000 0 18001800
  //   40000004 1 20800000 0 4800 8040 0 d000 10040 0 15800 18040 0 8020 4800 0 10020 d000 0 18020 15800 0
  //   10000000 40000000 0 8001800 0 8000004 280080 0 8000404 280080 0 8000804 280080 0 8000c04 280080 0
  //   8001004 280080 0 8001404 280080 0 8001804 280080 0 18001800 40000004 280080 0 10000000 40000004
  //   280080 0 10000000 40000000 0 10000000 40000000 0 10000000 40000000 0 10000000 40000000 0 10000000
  //   40000000 0 10000000 40000000 0 10000000 40000000 0 10000000 40000000 0 10000000 40000004 10000000
  //   20000000 800000 0 10000000 0 40000004 10000000 20000000 800000 0 10000000 0 40000004 10000000
  //   20000000 800000 0 10000000 0 40000004 10000000 20000000 800000 0 10000000 0 40000004 10000000
  //   20000000 800000 0 10000000 0 40000004 10000000 20000000 800000 0 10000000 0 40000004 10000000
  //   20000000 800000 0 10000000 0 40000004 10000000 20000000 800000 0 10000000 0 40000004 10000000
  //   20000000 800000 0 10000000 40000000 0 0 10000000 40000000 0 0 10000000 40000000 0 0 10000000
  //   40000000 0 0 10000000 40000000 0 0 10000000 40000000 0 0 10000000 40000000 0 0 10000000 40000000 0 0
  //   10000000 40000000 0 10000000 40000000 0 4 199880 6*0 10000000 28000400 0 10000000 2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
  //   contents of rom_2 (hex, n*v repeats v):
  //   48 0 0 0 80000000 4000 0 80000000 0 80000000 0 80000000 0 80000000 0 80000000 0 80000000 0 80000000
  //   0 0 80000000 0 80000000 0 80000000 0 80000000 0 80000000 0 80000000 0 80000000 0 80000000 0 0
  //   80000000 0 80000000 0 80000000 0 80000000 0 80000000 0 80000000 0 80000000 0 80000000 0 0 80000000 0
  //   80000000 0 80000000 0 80000000 0 80000000 0 80000000 0 80000000 0 80000000 0 0 80000000 0 80000000 0
  //   80000000 0 80000000 0 80000000 0 80000000 0 80000000 0 80000000 0 0 80000000 0 80000000 0 80000000 0
  //   80000000 0 80000000 0 80000000 0 80000000 0 80000000 0 0 80000000 0 80000000 0 80000000 0 80000000 0
  //   80000000 0 80000000 0 80000000 0 80000000 0 0 80000000 0 0 80000000 0 0 80000000 0 0 80000000 0 0
  //   80000000 0 0 80000000 0 0 80000000 0 0 80000000 40 8 80000000 40 8 80000000 40 8 80000000 40 8
  //   80000000 40 8 80000000 40 8 80000000 40 8 80000000 40 8 40 8 80000000 40 8 40 8 80000000 40 8 40 8
  //   80000000 0 0 80000000 0 0 80000000 40 0 8 40 0 8 80000000 40 0 8 80000000 40 0 0 80000000 0 0
  //   80000000 40 0 8000 8 80000000 6*0 80000000 0 80000000 0 80000000 0 10000 80000000 0 10000 80000000 0
  //   10000 80000000 0 10000 80000000 0 10000 80000000 0 10000 80000000 0 10000 80000000 0 0 10000
  //   80000000 0 10000 20000 80000000 0 10000 20000 80000000 0 10000 20000 80000000 0 10000 20000 80000000
  //   0 10000 20000 80000000 0 10000 20000 80000000 0 10000 20000 80000000 0 0 10000 20000 80000000 0
  //   10000 80000000 0 10000 80000000 0 10000 80000000 0 10000 80000000 0 10000 80000000 0 10000 80000000
  //   0 10000 80000000 0 0 10000 80000000 0 10000 40000 80000000 0 10000 40000 80000000 0 10000 40000
  //   80000000 0 10000 40000 80000000 0 10000 40000 80000000 0 10000 40000 80000000 0 10000 40000 80000000
  //   0 0 10000 40000 80000000 0 10000 20000 0 10000 20000 80000000 0 10000 20000 0 10000 20000 80000000 0
  //   10000 20000 0 10000 20000 80000000 48 0 10000 80000000 48 0 10000 20000 80000000 48 0 10000 80000000
  //   48 0 10000 40000 80000000 10000 80000000 0 10000 80000000 0 10000 80000000 0 10000 80000000 0 10000
  //   80000000 0 10000 80000000 0 10000 80000000 0 10000 80000000 0 0 10000 80000000 0 10000 80000000 0
  //   10000 80000000 0 10000 80000000 0 10000 80000000 0 10000 80000000 0 10000 80000000 0 10000 80000000
  //   0 0 10000 80000000 0 10000 80000000 0 10000 80000000 0 10000 80000000 0 10000 80000000 0 10000
  //   80000000 0 10000 80000000 0 10000 80000000 0 0 10000 80000000 48 0 10000 80000000 48 0 10000
  //   80000000 48 0 10000 80000000 10000 80000000 180000 510000 410000 80800000 180000 310000 210000
  //   80800000 0 80000000 0 80000000 0 80000000 0 80000000 0 80000000 0 80000000 0 80000000 0 80000000 0
  //   80000000 0 80000000 0 80000000 0 80000000 0 80000000 0 80000000 0 80000000 0 80000000 4*0 80000000
  //   4*0 80000000 2000000 0 80000000 2000000 0 80000000 2000000 0 80000000 0 1000000 80000000 0 1000000
  //   80000000 0 1000000 80000000 40 4000000 80000000 4000000 80000000 0 10000 80000000 0 10000 80000000 0
  //   10000 80000000 0 10000 80000000 0 10000 80000000 0 10000 80000000 0 10000 80000000 0 0 10000
  //   80000000 48 0 10000 80000000 40 100 80000000 48 200 80000000 48 8000000 80000000 48 800 80000000 48
  //   2000 80000000 48 1000 80000000 48 10000000 80000000 48 400 80000000 48 30 80 40 4000000 80000000 48
  //   20000200 30 80 40 4000000 80000000 48 20000100 30 80 40 4000000 80000000 48 20000800 30 80 40
  //   4000000 80000000 48 28000000 30 80 40 4000000 80000000 48 20001000 30 80 40 4000000 80000000 48 0 30
  //   80 40 4000000 80000000 48 30000000 30 80 40 4000000 80000000 48 20000400 30 80 40 4000000 80000000
  //   a0 4000000 80000000 20000200 a0 4000000 80000000 20000100 a0 4000000 80000000 20000800 a0 4000000
  //   80000000 28000000 a0 4000000 80000000 20001000 a0 4000000 80000000 20002000 a0 4000000 80000000
  //   30000000 a0 4000000 80000000 20000400 a0 4000000 80000000 40 10 80000000 80 10000 80000000 20
  //   80000000 30 80000000 30 80 0 30 80 0 80000000 30 80 0 30 80 0 80000000 30 80 0 30 80 0 80000000 0 30
  //   80 0 30 80 0 80000000 80 20 80 20 80000000 80 20 80 20 80000000 80 20 80 20 80000000 80 20 80 20
  //   80000000 80 0 0 20 80 0 0 20 80000000 10 80000000 3 80000000 4 80000000 0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
endmodule

module BCD (
  input  [15:0] in_1,
  output [15:0] out_2
);

  wire and_1_out, and_8_out, and_9_out, and_10_out, and_11_out, and_12_out, and_13_out, and_14_out,
       and_15_out, and_16_out, and_17_out, and_18_out, and_19_out, and_20_out, and_21_out, and_22_out,
       and_23_out, and_24_out, and_25_out, and_26_out, and_27_out, and_28_out, and_29_out, and_30_out,
       and_31_out, and_32_out, and_33_out, and_34_out, and_35_out, and_36_out, and_37_out, comparator_1_eq,
       comparator_1_gt, comparator_1_lt, comparator_2_eq, comparator_2_gt, comparator_2_lt, comparator_3_eq,
       comparator_3_gt, comparator_3_lt, comparator_4_gt, comparator_5_gt, comparator_6_gt, comparator_7_eq,
       comparator_7_gt, comparator_8_eq, comparator_8_gt, comparator_9_eq, comparator_9_gt, comparator_10_eq,
       comparator_10_gt, comparator_11_eq, comparator_11_gt, comparator_12_eq, comparator_12_gt,
       comparator_13_eq, comparator_13_gt, comparator_14_eq, comparator_14_gt, comparator_15_eq,
       comparator_15_gt, comparator_16_lt, comparator_17_lt, comparator_18_lt, comparator_19_lt,
       comparator_20_lt, comparator_21_lt, comparator_22_lt, comparator_23_lt, comparator_24_lt,
       comparator_25_eq, comparator_25_gt, comparator_26_eq, comparator_26_gt, comparator_27_eq,
       comparator_27_gt, comparator_28_eq, comparator_28_gt, comparator_29_eq, comparator_29_gt,
       comparator_30_eq, comparator_30_gt, comparator_31_eq, comparator_31_gt, comparator_32_eq,
       comparator_32_gt, comparator_33_eq, comparator_33_gt, comparator_34_lt, comparator_35_lt,
       comparator_36_lt, comparator_37_lt, comparator_38_lt, comparator_39_lt, comparator_40_lt,
       comparator_41_lt, comparator_42_lt, comparator_43_eq, comparator_43_gt, comparator_44_eq,
       comparator_44_gt, comparator_45_eq, comparator_45_gt, comparator_46_eq, comparator_46_gt,
       comparator_47_eq, comparator_47_gt, comparator_48_eq, comparator_48_gt, comparator_49_eq,
       comparator_49_gt, comparator_50_eq, comparator_50_gt, comparator_51_eq, comparator_51_gt,
       comparator_52_lt, comparator_53_lt, comparator_54_lt, comparator_55_lt, comparator_56_lt,
       comparator_57_lt, comparator_58_lt, comparator_59_lt, comparator_60_lt, comparator_61_eq,
       comparator_61_gt, comparator_61_lt, not_4_out, not_5_out, not_6_out, not_7_out, not_8_out, not_9_out,
       not_10_out, not_11_out, not_12_out, not_13_out, not_14_out, not_15_out, not_16_out, not_17_out,
       not_18_out, not_19_out, not_20_out, not_21_out, not_22_out, not_23_out, not_24_out, not_25_out,
       not_26_out, not_27_out, not_28_out, not_29_out, not_30_out, or_4_out, or_5_out, or_6_out, or_7_out,
       or_8_out, or_9_out, or_10_out, or_11_out, or_12_out, or_13_out, or_14_out, or_15_out, or_16_out,
       or_17_out, or_18_out, or_19_out, or_20_out, or_21_out, or_22_out, or_23_out, or_24_out, or_25_out,
       or_26_out, or_27_out, or_28_out, or_29_out, or_30_out, or_31_out, or_32_out, or_33_out, or_34_out;
  wire [15:0] and_2_out, and_3_out, and_4_out, and_5_out, and_6_out, and_7_out, controlled_buffer_1_out,
       controlled_buffer_5_out, controlled_buffer_14_out, controlled_buffer_23_out, controlled_buffer_33_out,
       controlled_buffer_45_out, controlled_buffer_55_out, controlled_buffer_57_out, not_1_out, not_2_out,
       not_3_out, subtractor_1_out, subtractor_2_out, subtractor_3_out, subtractor_4_out, subtractor_5_out,
       subtractor_6_out, subtractor_7_out, subtractor_8_out, subtractor_9_out, subtractor_10_out,
       subtractor_11_out, subtractor_12_out, subtractor_13_out, subtractor_14_out, subtractor_15_out,
       subtractor_16_out, subtractor_17_out, subtractor_18_out, subtractor_19_out, subtractor_20_out,
       subtractor_21_out, subtractor_22_out, subtractor_23_out, subtractor_24_out, subtractor_25_out,
       subtractor_26_out, subtractor_27_out, subtractor_28_out, subtractor_29_out, subtractor_30_out;
  wire [15:15] or_1_out, or_2_out, or_3_out;

  Comparator #(.width(16)) comparator_1 (
    .a(in_1), .b(16'h7530), .gt(comparator_1_gt), .eq(comparator_1_eq), .lt(comparator_1_lt));
  Comparator #(.width(16)) comparator_2 (
    .a(in_1), .b(16'h4e20), .gt(comparator_2_gt), .eq(comparator_2_eq), .lt(comparator_2_lt));
  Comparator #(.width(16)) comparator_3 (
    .a(in_1), .b(16'h2710), .gt(comparator_3_gt), .eq(comparator_3_eq), .lt(comparator_3_lt));
  and and_1 (and_1_out, comparator_3_lt, comparator_2_lt, comparator_1_lt);
  or or_1 (or_1_out[15], comparator_1_gt, comparator_1_eq);
  or or_2 (or_2_out[15], comparator_2_gt, comparator_2_eq);
  or or_3 (or_3_out[15], comparator_3_gt, comparator_3_eq);
  assign controlled_buffer_1_out = and_1_out ? in_1 : 16'bz;  // Controlled_Buffer controlled_buffer_1
  assign and_2_out = {16{or_1_out[15]}} & in_1;  // AND_Gate and_2, 16 bits wide
  assign and_3_out = {16{or_2_out[15]}} & in_1;  // AND_Gate and_3, 16 bits wide
  assign and_4_out = {16{or_3_out[15]}} & in_1;  // AND_Gate and_4, 16 bits wide
  assign and_5_out = and_2_out & and_3_out & and_4_out;  // AND_Gate and_5, 16 bits wide
  assign not_1_out = ~and_2_out;  // NOT_Gate not_1, 16 bits wide
  assign and_6_out = and_3_out & not_1_out & and_4_out;  // AND_Gate and_6, 16 bits wide
  assign not_2_out = ~and_2_out;  // NOT_Gate not_2, 16 bits wide
  assign and_7_out = and_4_out & not_2_out & not_3_out;  // AND_Gate and_7, 16 bits wide
  assign not_3_out = ~and_3_out;  // NOT_Gate not_3, 16 bits wide
  Subtractor #(.width(16)) subtractor_1 (.a(and_5_out), .b(16'h7530), .out(subtractor_1_out));  // open: bin, bout
  Subtractor #(.width(16)) subtractor_2 (.a(and_6_out), .b(16'h4e20), .out(subtractor_2_out));  // open: bin, bout
  Subtractor #(.width(16)) subtractor_3 (.a(and_7_out), .b(16'h2710), .out(subtractor_3_out));  // open: bin, bout
  Comparator #(.width(16)) comparator_4 (.a(subtractor_1_out), .b({16{1'b0}}), .gt(comparator_4_gt));  // open: eq, lt
  Comparator #(.width(16)) comparator_5 (.a(subtractor_2_out), .b({16{1'b0}}), .gt(comparator_5_gt));  // open: eq, lt
  Comparator #(.width(16)) comparator_6 (.a(subtractor_3_out), .b({16{1'b0}}), .gt(comparator_6_gt));  // open: eq, lt
  assign controlled_buffer_1_out = comparator_4_gt ? subtractor_1_out : 16'bz;  // Controlled_Buffer controlled_buffer_2
  assign controlled_buffer_1_out = comparator_5_gt ? subtractor_2_out : 16'bz;  // Controlled_Buffer controlled_buffer_3
  assign controlled_buffer_1_out = comparator_6_gt ? subtractor_3_out : 16'bz;  // Controlled_Buffer controlled_buffer_4
  Subtractor #(.width(16)) subtractor_4 (
    .a(controlled_buffer_23_out), .b(16'h384), .out(subtractor_4_out));  // open: bin, bout
  Subtractor #(.width(16)) subtractor_5 (
    .a(controlled_buffer_23_out), .b(16'h320), .out(subtractor_5_out));  // open: bin, bout
  Subtractor #(.width(16)) subtractor_6 (
    .a(controlled_buffer_23_out), .b(16'h2bc), .out(subtractor_6_out));  // open: bin, bout
  Subtractor #(.width(16)) subtractor_7 (
    .a(controlled_buffer_23_out), .b(16'h258), .out(subtractor_7_out));  // open: bin, bout
  Subtractor #(.width(16)) subtractor_8 (
    .a(controlled_buffer_23_out), .b(16'h1f4), .out(subtractor_8_out));  // open: bin, bout
  Subtractor #(.width(16)) subtractor_9 (
    .a(controlled_buffer_23_out), .b(16'h190), .out(subtractor_9_out));  // open: bin, bout
  Subtractor #(.width(16)) subtractor_10 (
    .a(controlled_buffer_23_out), .b(16'h12c), .out(subtractor_10_out));  // open: bin, bout
  Subtractor #(.width(16)) subtractor_11 (
    .a(controlled_buffer_23_out), .b(16'hc8), .out(subtractor_11_out));  // open: bin, bout
  Subtractor #(.width(16)) subtractor_12 (
    .a(controlled_buffer_23_out), .b(16'h64), .out(subtractor_12_out));  // open: bin, bout
  Subtractor #(.width(16)) subtractor_13 (
    .a(controlled_buffer_5_out), .b(16'h5a), .out(subtractor_13_out));  // open: bin, bout
  Subtractor #(.width(16)) subtractor_14 (
    .a(controlled_buffer_5_out), .b(16'h50), .out(subtractor_14_out));  // open: bin, bout
  Subtractor #(.width(16)) subtractor_15 (
    .a(controlled_buffer_5_out), .b(16'h46), .out(subtractor_15_out));  // open: bin, bout
  Subtractor #(.width(16)) subtractor_16 (
    .a(controlled_buffer_5_out), .b(16'h3c), .out(subtractor_16_out));  // open: bin, bout
  Subtractor #(.width(16)) subtractor_17 (
    .a(controlled_buffer_5_out), .b(16'h32), .out(subtractor_17_out));  // open: bin, bout
  Subtractor #(.width(16)) subtractor_18 (
    .a(controlled_buffer_5_out), .b(16'h28), .out(subtractor_18_out));  // open: bin, bout
  Subtractor #(.width(16)) subtractor_19 (
    .a(controlled_buffer_5_out), .b(16'h1e), .out(subtractor_19_out));  // open: bin, bout
  Subtractor #(.width(16)) subtractor_20 (
    .a(controlled_buffer_5_out), .b(16'h14), .out(subtractor_20_out));  // open: bin, bout
  Subtractor #(.width(16)) subtractor_21 (
    .a(controlled_buffer_5_out), .b(16'ha), .out(subtractor_21_out));  // open: bin, bout
  Subtractor #(.width(16)) subtractor_22 (
    .a(controlled_buffer_1_out), .b(16'h2328), .out(subtractor_22_out));  // open: bin, bout
  Subtractor #(.width(16)) subtractor_23 (
    .a(controlled_buffer_1_out), .b(16'h1f40), .out(subtractor_23_out));  // open: bin, bout
  Subtractor #(.width(16)) subtractor_24 (
    .a(controlled_buffer_1_out), .b(16'h1b58), .out(subtractor_24_out));  // open: bin, bout
  Subtractor #(.width(16)) subtractor_25 (
    .a(controlled_buffer_1_out), .b(16'h1770), .out(subtractor_25_out));  // open: bin, bout
  Subtractor #(.width(16)) subtractor_26 (
    .a(controlled_buffer_1_out), .b(16'h1388), .out(subtractor_26_out));  // open: bin, bout
  Subtractor #(.width(16)) subtractor_27 (
    .a(controlled_buffer_1_out), .b(16'hfa0), .out(subtractor_27_out));  // open: bin, bout
  Subtractor #(.width(16)) subtractor_28 (
    .a(controlled_buffer_1_out), .b(16'hbb8), .out(subtractor_28_out));  // open: bin, bout
  Subtractor #(.width(16)) subtractor_29 (
    .a(controlled_buffer_1_out), .b(16'h7d0), .out(subtractor_29_out));  // open: bin, bout
  Subtractor #(.width(16)) subtractor_30 (
    .a(controlled_buffer_1_out), .b(16'h3e8), .out(subtractor_30_out));  // open: bin, bout
  Comparator #(.width(16)) comparator_7 (
    .a(subtractor_4_out), .b({16{1'b0}}), .gt(comparator_7_gt), .eq(comparator_7_eq));  // open: lt
  Comparator #(.width(16)) comparator_8 (
    .a(subtractor_5_out), .b({16{1'b0}}), .gt(comparator_8_gt), .eq(comparator_8_eq));  // open: lt
  and and_8 (and_8_out, comparator_8_gt, comparator_17_lt);
  Comparator #(.width(16)) comparator_9 (
    .a(subtractor_6_out), .b({16{1'b0}}), .gt(comparator_9_gt), .eq(comparator_9_eq));  // open: lt
  Comparator #(.width(16)) comparator_10 (
    .a(subtractor_7_out), .b({16{1'b0}}), .gt(comparator_10_gt), .eq(comparator_10_eq));  // open: lt
  and and_9 (and_9_out, comparator_10_gt, comparator_19_lt);
  Comparator #(.width(16)) comparator_11 (
    .a(subtractor_8_out), .b({16{1'b0}}), .gt(comparator_11_gt), .eq(comparator_11_eq));  // open: lt
  Comparator #(.width(16)) comparator_12 (
    .a(subtractor_9_out), .b({16{1'b0}}), .gt(comparator_12_gt), .eq(comparator_12_eq));  // open: lt
  and and_10 (and_10_out, comparator_12_gt, comparator_21_lt);
  Comparator #(.width(16)) comparator_13 (
    .a(subtractor_10_out), .b({16{1'b0}}), .gt(comparator_13_gt), .eq(comparator_13_eq));  // open: lt
  Comparator #(.width(16)) comparator_14 (
    .a(subtractor_11_out), .b({16{1'b0}}), .gt(comparator_14_gt), .eq(comparator_14_eq));  // open: lt
  and and_11 (and_11_out, comparator_14_gt, comparator_23_lt);
  Comparator #(.width(16)) comparator_15 (
    .a(subtractor_12_out), .b({16{1'b0}}), .gt(comparator_15_gt), .eq(comparator_15_eq));  // open: lt
  Comparator #(.width(16)) comparator_16 (.a(subtractor_4_out), .b(16'h64), .lt(comparator_16_lt));  // open: gt, eq
  Comparator #(.width(16)) comparator_17 (.a(subtractor_5_out), .b(16'h64), .lt(comparator_17_lt));  // open: gt, eq
  Comparator #(.width(16)) comparator_18 (.a(subtractor_6_out), .b(16'h64), .lt(comparator_18_lt));  // open: gt, eq
  Comparator #(.width(16)) comparator_19 (.a(subtractor_7_out), .b(16'h64), .lt(comparator_19_lt));  // open: gt, eq
  Comparator #(.width(16)) comparator_20 (.a(subtractor_8_out), .b(16'h64), .lt(comparator_20_lt));  // open: gt, eq
  Comparator #(.width(16)) comparator_21 (.a(subtractor_9_out), .b(16'h64), .lt(comparator_21_lt));  // open: gt, eq
  Comparator #(.width(16)) comparator_22 (.a(subtractor_10_out), .b(16'h64), .lt(comparator_22_lt));  // open: gt, eq
  Comparator #(.width(16)) comparator_23 (.a(subtractor_11_out), .b(16'h64), .lt(comparator_23_lt));  // open: gt, eq
  Comparator #(.width(16)) comparator_24 (.a(subtractor_12_out), .b(16'h64), .lt(comparator_24_lt));  // open: gt, eq
  and and_12 (and_12_out, comparator_7_gt, comparator_16_lt);
  and and_13 (and_13_out, comparator_9_gt, comparator_18_lt);
  and and_14 (and_14_out, comparator_11_gt, comparator_20_lt);
  and and_15 (and_15_out, comparator_13_gt, comparator_22_lt);
  and and_16 (and_16_out, comparator_15_gt, comparator_24_lt);
  Comparator #(.width(16)) comparator_25 (
    .a(subtractor_13_out), .b({16{1'b0}}), .gt(comparator_25_gt), .eq(comparator_25_eq));  // open: lt
  Comparator #(.width(16)) comparator_26 (
    .a(subtractor_14_out), .b({16{1'b0}}), .gt(comparator_26_gt), .eq(comparator_26_eq));  // open: lt
  and and_17 (and_17_out, comparator_26_gt, comparator_35_lt);
  Comparator #(.width(16)) comparator_27 (
    .a(subtractor_15_out), .b({16{1'b0}}), .gt(comparator_27_gt), .eq(comparator_27_eq));  // open: lt
  Comparator #(.width(16)) comparator_28 (
    .a(subtractor_16_out), .b({16{1'b0}}), .gt(comparator_28_gt), .eq(comparator_28_eq));  // open: lt
  and and_18 (and_18_out, comparator_28_gt, comparator_37_lt);
  Comparator #(.width(16)) comparator_29 (
    .a(subtractor_17_out), .b({16{1'b0}}), .gt(comparator_29_gt), .eq(comparator_29_eq));  // open: lt
  Comparator #(.width(16)) comparator_30 (
    .a(subtractor_18_out), .b({16{1'b0}}), .gt(comparator_30_gt), .eq(comparator_30_eq));  // open: lt
  and and_19 (and_19_out, comparator_30_gt, comparator_39_lt);
  Comparator #(.width(16)) comparator_31 (
    .a(subtractor_19_out), .b({16{1'b0}}), .gt(comparator_31_gt), .eq(comparator_31_eq));  // open: lt
  Comparator #(.width(16)) comparator_32 (
    .a(subtractor_20_out), .b({16{1'b0}}), .gt(comparator_32_gt), .eq(comparator_32_eq));  // open: lt
  and and_20 (and_20_out, comparator_32_gt, comparator_41_lt);
  Comparator #(.width(16)) comparator_33 (
    .a(subtractor_21_out), .b({16{1'b0}}), .gt(comparator_33_gt), .eq(comparator_33_eq));  // open: lt
  Comparator #(.width(16)) comparator_34 (.a(subtractor_13_out), .b(16'ha), .lt(comparator_34_lt));  // open: gt, eq
  Comparator #(.width(16)) comparator_35 (.a(subtractor_14_out), .b(16'ha), .lt(comparator_35_lt));  // open: gt, eq
  Comparator #(.width(16)) comparator_36 (.a(subtractor_15_out), .b(16'ha), .lt(comparator_36_lt));  // open: gt, eq
  Comparator #(.width(16)) comparator_37 (.a(subtractor_16_out), .b(16'ha), .lt(comparator_37_lt));  // open: gt, eq
  Comparator #(.width(16)) comparator_38 (.a(subtractor_17_out), .b(16'ha), .lt(comparator_38_lt));  // open: gt, eq
  Comparator #(.width(16)) comparator_39 (.a(subtractor_18_out), .b(16'ha), .lt(comparator_39_lt));  // open: gt, eq
  Comparator #(.width(16)) comparator_40 (.a(subtractor_19_out), .b(16'ha), .lt(comparator_40_lt));  // open: gt, eq
  Comparator #(.width(16)) comparator_41 (.a(subtractor_20_out), .b(16'ha), .lt(comparator_41_lt));  // open: gt, eq
  Comparator #(.width(16)) comparator_42 (.a(subtractor_21_out), .b(16'ha), .lt(comparator_42_lt));  // open: gt, eq
  Comparator #(.width(16)) comparator_43 (
    .a(subtractor_22_out), .b({16{1'b0}}), .gt(comparator_43_gt), .eq(comparator_43_eq));  // open: lt
  Comparator #(.width(16)) comparator_44 (
    .a(subtractor_23_out), .b({16{1'b0}}), .gt(comparator_44_gt), .eq(comparator_44_eq));  // open: lt
  Comparator #(.width(16)) comparator_45 (
    .a(subtractor_24_out), .b({16{1'b0}}), .gt(comparator_45_gt), .eq(comparator_45_eq));  // open: lt
  Comparator #(.width(16)) comparator_46 (
    .a(subtractor_25_out), .b({16{1'b0}}), .gt(comparator_46_gt), .eq(comparator_46_eq));  // open: lt
  Comparator #(.width(16)) comparator_47 (
    .a(subtractor_26_out), .b({16{1'b0}}), .gt(comparator_47_gt), .eq(comparator_47_eq));  // open: lt
  Comparator #(.width(16)) comparator_48 (
    .a(subtractor_27_out), .b({16{1'b0}}), .gt(comparator_48_gt), .eq(comparator_48_eq));  // open: lt
  and and_21 (and_21_out, comparator_48_gt, comparator_57_lt);
  Comparator #(.width(16)) comparator_49 (
    .a(subtractor_28_out), .b({16{1'b0}}), .gt(comparator_49_gt), .eq(comparator_49_eq));  // open: lt
  Comparator #(.width(16)) comparator_50 (
    .a(subtractor_29_out), .b({16{1'b0}}), .gt(comparator_50_gt), .eq(comparator_50_eq));  // open: lt
  and and_22 (and_22_out, comparator_50_gt, comparator_59_lt);
  Comparator #(.width(16)) comparator_51 (
    .a(subtractor_30_out), .b({16{1'b0}}), .gt(comparator_51_gt), .eq(comparator_51_eq));  // open: lt
  Comparator #(.width(16)) comparator_52 (.a(subtractor_22_out), .b(16'h3e8), .lt(comparator_52_lt));  // open: gt, eq
  Comparator #(.width(16)) comparator_53 (.a(subtractor_23_out), .b(16'h3e8), .lt(comparator_53_lt));  // open: gt, eq
  Comparator #(.width(16)) comparator_54 (.a(subtractor_24_out), .b(16'h3e8), .lt(comparator_54_lt));  // open: gt, eq
  Comparator #(.width(16)) comparator_55 (.a(subtractor_25_out), .b(16'h3e8), .lt(comparator_55_lt));  // open: gt, eq
  Comparator #(.width(16)) comparator_56 (.a(subtractor_26_out), .b(16'h3e8), .lt(comparator_56_lt));  // open: gt, eq
  Comparator #(.width(16)) comparator_57 (.a(subtractor_27_out), .b(16'h3e8), .lt(comparator_57_lt));  // open: gt, eq
  Comparator #(.width(16)) comparator_58 (.a(subtractor_28_out), .b(16'h3e8), .lt(comparator_58_lt));  // open: gt, eq
  Comparator #(.width(16)) comparator_59 (.a(subtractor_29_out), .b(16'h3e8), .lt(comparator_59_lt));  // open: gt, eq
  Comparator #(.width(16)) comparator_60 (.a(subtractor_30_out), .b(16'h3e8), .lt(comparator_60_lt));  // open: gt, eq
  and and_23 (and_23_out, comparator_25_gt, comparator_34_lt);
  and and_24 (and_24_out, comparator_27_gt, comparator_36_lt);
  and and_25 (and_25_out, comparator_29_gt, comparator_38_lt);
  and and_26 (and_26_out, comparator_31_gt, comparator_40_lt);
  and and_27 (and_27_out, comparator_33_gt, comparator_42_lt);
  and and_28 (and_28_out, comparator_43_gt, comparator_52_lt);
  and and_29 (and_29_out, comparator_44_gt, comparator_53_lt);
  and and_30 (and_30_out, comparator_45_gt, comparator_54_lt);
  and and_31 (and_31_out, comparator_46_gt, comparator_55_lt);
  and and_32 (and_32_out, comparator_47_gt, comparator_56_lt);
  and and_33 (and_33_out, comparator_49_gt, comparator_58_lt);
  and and_34 (and_34_out, comparator_51_gt, comparator_60_lt);
  assign controlled_buffer_5_out = and_12_out ? subtractor_4_out : 16'bz;  // Controlled_Buffer controlled_buffer_5
  assign controlled_buffer_5_out = and_8_out ? subtractor_5_out : 16'bz;  // Controlled_Buffer controlled_buffer_6
  assign controlled_buffer_5_out = and_13_out ? subtractor_6_out : 16'bz;  // Controlled_Buffer controlled_buffer_7
  assign controlled_buffer_5_out = and_9_out ? subtractor_7_out : 16'bz;  // Controlled_Buffer controlled_buffer_8
  assign controlled_buffer_5_out = and_14_out ? subtractor_8_out : 16'bz;  // Controlled_Buffer controlled_buffer_9
  assign controlled_buffer_5_out = and_10_out ? subtractor_9_out : 16'bz;  // Controlled_Buffer controlled_buffer_10
  assign controlled_buffer_5_out = and_15_out ? subtractor_10_out : 16'bz;  // Controlled_Buffer controlled_buffer_11
  assign controlled_buffer_5_out = and_11_out ? subtractor_11_out : 16'bz;  // Controlled_Buffer controlled_buffer_12
  assign controlled_buffer_5_out = and_16_out ? subtractor_12_out : 16'bz;  // Controlled_Buffer controlled_buffer_13
  or or_4 (or_4_out, comparator_7_eq, and_12_out);
  or or_5 (or_5_out, comparator_8_eq, and_8_out);
  or or_6 (or_6_out, and_13_out, comparator_9_eq);
  or or_7 (or_7_out, comparator_10_eq, and_9_out);
  or or_8 (or_8_out, comparator_11_eq, and_14_out);
  or or_9 (or_9_out, comparator_12_eq, and_10_out);
  or or_10 (or_10_out, and_15_out, comparator_13_eq);
  or or_11 (or_11_out, and_11_out, comparator_14_eq);
  or or_12 (or_12_out, comparator_15_eq, and_16_out);
  assign controlled_buffer_14_out = and_23_out ? subtractor_13_out : 16'bz;  // Controlled_Buffer controlled_buffer_14
  assign controlled_buffer_14_out = and_17_out ? subtractor_14_out : 16'bz;  // Controlled_Buffer controlled_buffer_15
  assign controlled_buffer_14_out = and_24_out ? subtractor_15_out : 16'bz;  // Controlled_Buffer controlled_buffer_16
  assign controlled_buffer_14_out = and_18_out ? subtractor_16_out : 16'bz;  // Controlled_Buffer controlled_buffer_17
  assign controlled_buffer_14_out = and_25_out ? subtractor_17_out : 16'bz;  // Controlled_Buffer controlled_buffer_18
  assign controlled_buffer_14_out = and_19_out ? subtractor_18_out : 16'bz;  // Controlled_Buffer controlled_buffer_19
  assign controlled_buffer_14_out = and_26_out ? subtractor_19_out : 16'bz;  // Controlled_Buffer controlled_buffer_20
  assign controlled_buffer_14_out = and_20_out ? subtractor_20_out : 16'bz;  // Controlled_Buffer controlled_buffer_21
  assign controlled_buffer_14_out = and_27_out ? subtractor_21_out : 16'bz;  // Controlled_Buffer controlled_buffer_22
  assign controlled_buffer_23_out = and_28_out ? subtractor_22_out : 16'bz;  // Controlled_Buffer controlled_buffer_23
  assign controlled_buffer_23_out = and_29_out ? subtractor_23_out : 16'bz;  // Controlled_Buffer controlled_buffer_24
  assign controlled_buffer_23_out = and_30_out ? subtractor_24_out : 16'bz;  // Controlled_Buffer controlled_buffer_25
  assign controlled_buffer_23_out = and_31_out ? subtractor_25_out : 16'bz;  // Controlled_Buffer controlled_buffer_26
  assign controlled_buffer_23_out = and_32_out ? subtractor_26_out : 16'bz;  // Controlled_Buffer controlled_buffer_27
  assign controlled_buffer_23_out = and_21_out ? subtractor_27_out : 16'bz;  // Controlled_Buffer controlled_buffer_28
  assign controlled_buffer_23_out = and_33_out ? subtractor_28_out : 16'bz;  // Controlled_Buffer controlled_buffer_29
  assign controlled_buffer_23_out = and_22_out ? subtractor_29_out : 16'bz;  // Controlled_Buffer controlled_buffer_30
  assign controlled_buffer_23_out = and_34_out ? subtractor_30_out : 16'bz;  // Controlled_Buffer controlled_buffer_31
  not not_4 (not_4_out, or_8_out);
  not not_5 (not_5_out, or_11_out);
  not not_6 (not_6_out, or_7_out);
  not not_7 (not_7_out, or_9_out);
  not not_8 (not_8_out, or_6_out);
  not not_9 (not_9_out, or_4_out);
  not not_10 (not_10_out, or_10_out);
  not not_11 (not_11_out, or_5_out);
  and and_35 (and_35_out, not_9_out, not_11_out, not_8_out, not_6_out, not_4_out, not_7_out, not_10_out, not_5_out, not_14_out);
  or or_13 (or_13_out, comparator_7_eq, comparator_8_eq, comparator_9_eq, comparator_10_eq, comparator_11_eq, comparator_12_eq, comparator_13_eq, comparator_14_eq, comparator_15_eq, and_35_out);
  assign controlled_buffer_5_out = or_13_out ? controlled_buffer_23_out : 16'bz;  // Controlled_Buffer controlled_buffer_32
  or or_14 (or_14_out, comparator_25_eq, and_23_out);
  or or_15 (or_15_out, comparator_26_eq, and_17_out);
  or or_16 (or_16_out, and_24_out, comparator_27_eq);
  or or_17 (or_17_out, comparator_28_eq, and_18_out);
  or or_18 (or_18_out, comparator_29_eq, and_25_out);
  or or_19 (or_19_out, comparator_30_eq, and_19_out);
  or or_20 (or_20_out, and_26_out, comparator_31_eq);
  or or_21 (or_21_out, and_20_out, comparator_32_eq);
  or or_22 (or_22_out, comparator_33_eq, and_27_out);
  not not_12 (not_12_out, or_15_out);
  not not_13 (not_13_out, or_14_out);
  or or_23 (or_23_out, comparator_25_eq, comparator_26_eq, comparator_27_eq, comparator_28_eq, comparator_29_eq, comparator_30_eq, comparator_31_eq, comparator_32_eq, comparator_33_eq, and_36_out);
  or or_24 (or_24_out, comparator_43_eq, and_28_out);
  or or_25 (or_25_out, comparator_44_eq, and_29_out);
  or or_26 (or_26_out, and_30_out, comparator_45_eq);
  or or_27 (or_27_out, comparator_46_eq, and_31_out);
  or or_28 (or_28_out, comparator_47_eq, and_32_out);
  or or_29 (or_29_out, comparator_48_eq, and_21_out);
  or or_30 (or_30_out, and_33_out, comparator_49_eq);
  or or_31 (or_31_out, and_22_out, comparator_50_eq);
  or or_32 (or_32_out, comparator_51_eq, and_34_out);
  assign controlled_buffer_33_out = or_4_out ? 16'h9 : 16'bz;  // Controlled_Buffer controlled_buffer_33
  assign controlled_buffer_33_out = or_5_out ? 16'h8 : 16'bz;  // Controlled_Buffer controlled_buffer_34
  assign controlled_buffer_33_out = or_6_out ? 16'h7 : 16'bz;  // Controlled_Buffer controlled_buffer_35
  assign controlled_buffer_33_out = or_7_out ? 16'h6 : 16'bz;  // Controlled_Buffer controlled_buffer_36
  assign controlled_buffer_33_out = or_8_out ? 16'h5 : 16'bz;  // Controlled_Buffer controlled_buffer_37
  assign controlled_buffer_33_out = or_9_out ? 16'h4 : 16'bz;  // Controlled_Buffer controlled_buffer_38
  assign controlled_buffer_33_out = or_10_out ? 16'h3 : 16'bz;  // Controlled_Buffer controlled_buffer_39
  assign controlled_buffer_33_out = or_11_out ? 16'h2 : 16'bz;  // Controlled_Buffer controlled_buffer_40
  assign controlled_buffer_33_out = or_12_out ? 16'h1 : 16'bz;  // Controlled_Buffer controlled_buffer_41
  not not_14 (not_14_out, or_12_out);
  assign controlled_buffer_33_out = and_35_out ? {16{1'b0}} : 16'bz;  // Controlled_Buffer controlled_buffer_42
  not not_15 (not_15_out, or_16_out);
  not not_16 (not_16_out, or_22_out);
  not not_17 (not_17_out, or_19_out);
  not not_18 (not_18_out, or_20_out);
  not not_19 (not_19_out, or_17_out);
  not not_20 (not_20_out, or_21_out);
  not not_21 (not_21_out, or_18_out);
  and and_36 (and_36_out, not_13_out, not_12_out, not_15_out, not_19_out, not_21_out, not_17_out, not_18_out, not_20_out, not_16_out);
  assign controlled_buffer_14_out = or_23_out ? controlled_buffer_5_out : 16'bz;  // Controlled_Buffer controlled_buffer_43
  Comparator #(.width(16)) comparator_61 (
    .a(controlled_buffer_14_out), .b(16'ha), .gt(comparator_61_gt), .eq(comparator_61_eq),
    .lt(comparator_61_lt));
  not not_22 (not_22_out, or_24_out);
  not not_23 (not_23_out, or_26_out);
  not not_24 (not_24_out, or_29_out);
  not not_25 (not_25_out, or_30_out);
  not not_26 (not_26_out, or_27_out);
  not not_27 (not_27_out, or_25_out);
  not not_28 (not_28_out, or_28_out);
  and and_37 (and_37_out, not_22_out, not_27_out, not_23_out, not_26_out, not_28_out, not_24_out, not_25_out, not_29_out, not_30_out);
  or or_33 (or_33_out, comparator_43_eq, comparator_44_eq, comparator_45_eq, comparator_46_eq, comparator_47_eq, comparator_48_eq, comparator_49_eq, comparator_50_eq, comparator_51_eq, and_37_out);
  assign controlled_buffer_23_out = or_33_out ? controlled_buffer_1_out : 16'bz;  // Controlled_Buffer controlled_buffer_44
  Bit_Extender #(.in_width(16), .out_width(4)) bit_extender_1 (.in(controlled_buffer_33_out), .out(out_2[11:8]));
  assign controlled_buffer_45_out = or_14_out ? 16'h9 : 16'bz;  // Controlled_Buffer controlled_buffer_45
  assign controlled_buffer_45_out = or_15_out ? 16'h8 : 16'bz;  // Controlled_Buffer controlled_buffer_46
  assign controlled_buffer_45_out = or_16_out ? 16'h7 : 16'bz;  // Controlled_Buffer controlled_buffer_47
  assign controlled_buffer_45_out = or_17_out ? 16'h6 : 16'bz;  // Controlled_Buffer controlled_buffer_48
  assign controlled_buffer_45_out = or_18_out ? 16'h5 : 16'bz;  // Controlled_Buffer controlled_buffer_49
  assign controlled_buffer_45_out = or_19_out ? 16'h4 : 16'bz;  // Controlled_Buffer controlled_buffer_50
  assign controlled_buffer_45_out = or_20_out ? 16'h3 : 16'bz;  // Controlled_Buffer controlled_buffer_51
  assign controlled_buffer_45_out = or_21_out ? 16'h2 : 16'bz;  // Controlled_Buffer controlled_buffer_52
  assign controlled_buffer_45_out = or_22_out ? 16'h1 : 16'bz;  // Controlled_Buffer controlled_buffer_53
  assign controlled_buffer_45_out = and_36_out ? {16{1'b0}} : 16'bz;  // Controlled_Buffer controlled_buffer_54
  assign controlled_buffer_55_out = or_34_out ? {16{1'b0}} : 16'bz;  // Controlled_Buffer controlled_buffer_55
  assign controlled_buffer_55_out = comparator_61_lt ? controlled_buffer_14_out : 16'bz;  // Controlled_Buffer controlled_buffer_56
  or or_34 (or_34_out, comparator_61_gt, comparator_61_eq);
  assign controlled_buffer_57_out = or_24_out ? 16'h9 : 16'bz;  // Controlled_Buffer controlled_buffer_57
  assign controlled_buffer_57_out = or_25_out ? 16'h8 : 16'bz;  // Controlled_Buffer controlled_buffer_58
  assign controlled_buffer_57_out = or_26_out ? 16'h7 : 16'bz;  // Controlled_Buffer controlled_buffer_59
  assign controlled_buffer_57_out = or_27_out ? 16'h6 : 16'bz;  // Controlled_Buffer controlled_buffer_60
  assign controlled_buffer_57_out = or_28_out ? 16'h5 : 16'bz;  // Controlled_Buffer controlled_buffer_61
  assign controlled_buffer_57_out = or_29_out ? 16'h4 : 16'bz;  // Controlled_Buffer controlled_buffer_62
  assign controlled_buffer_57_out = or_30_out ? 16'h3 : 16'bz;  // Controlled_Buffer controlled_buffer_63
  assign controlled_buffer_57_out = or_31_out ? 16'h2 : 16'bz;  // Controlled_Buffer controlled_buffer_64
  assign controlled_buffer_57_out = or_32_out ? 16'h1 : 16'bz;  // Controlled_Buffer controlled_buffer_65
  not not_29 (not_29_out, or_31_out);
  not not_30 (not_30_out, or_32_out);
  Bit_Extender #(.in_width(16), .out_width(4)) bit_extender_2 (.in(controlled_buffer_45_out), .out(out_2[7:4]));
  Bit_Extender #(.in_width(16), .out_width(4)) bit_extender_3 (.in(controlled_buffer_55_out), .out(out_2[3:0]));
  Bit_Extender #(.in_width(16), .out_width(4)) bit_extender_4 (.in(controlled_buffer_57_out), .out(out_2[15:12]));
  assign controlled_buffer_57_out = and_37_out ? {16{1'b0}} : 16'bz;  // Controlled_Buffer controlled_buffer_66
endmodule

module ScreenDriver (
  input  [31:0] in_1,
  input  [4:0] in_2,
  input  in_3,
  input  in_4,
  input  in_5,
  output [31:0] out_6,
  output [31:0] out_7,
  output [31:0] out_8,
  output [31:0] out_9,
  output [31:0] out_10,
  output [31:0] out_11,
  output [31:0] out_12,
  output [31:0] out_13,
  output [31:0] out_14,
  output [31:0] out_15,
  output [31:0] out_16,
  output [31:0] out_17,
  output [31:0] out_18,
  output [31:0] out_19,
  output [31:0] out_20,
  output [31:0] out_21,
  output [31:0] out_22,
  output [31:0] out_23,
  output [31:0] out_24,
  output [31:0] out_25,
  output [31:0] out_26,
  output [31:0] out_27,
  output [31:0] out_28,
  output [31:0] out_29,
  output [31:0] out_30,
  output [31:0] out_31,
  output [31:0] out_32,
  output [31:0] out_33,
  output [31:0] out_34,
  output [31:0] out_35,
  output [31:0] out_36,
  output [31:0] out_37
);

  wire demultiplexer_2_out0, demultiplexer_2_out1, demultiplexer_2_out2, demultiplexer_2_out3,
       demultiplexer_2_out4, demultiplexer_2_out5, demultiplexer_2_out6, demultiplexer_2_out7,
       demultiplexer_2_out8, demultiplexer_2_out9, demultiplexer_2_out10, demultiplexer_2_out11,
       demultiplexer_2_out12, demultiplexer_2_out13, demultiplexer_2_out14, demultiplexer_2_out15,
       demultiplexer_2_out16, demultiplexer_2_out17, demultiplexer_2_out18, demultiplexer_2_out19,
       demultiplexer_2_out20, demultiplexer_2_out21, demultiplexer_2_out22, demultiplexer_2_out23,
       demultiplexer_2_out24, demultiplexer_2_out25, demultiplexer_2_out26, demultiplexer_2_out27,
       demultiplexer_2_out28, demultiplexer_2_out29, demultiplexer_2_out30, demultiplexer_2_out31;
  wire [31:0] demultiplexer_1_out0, demultiplexer_1_out1, demultiplexer_1_out2, demultiplexer_1_out3,
       demultiplexer_1_out4, demultiplexer_1_out5, demultiplexer_1_out6, demultiplexer_1_out7,
       demultiplexer_1_out8, demultiplexer_1_out9, demultiplexer_1_out10, demultiplexer_1_out11,
       demultiplexer_1_out12, demultiplexer_1_out13, demultiplexer_1_out14, demultiplexer_1_out15,
       demultiplexer_1_out16, demultiplexer_1_out17, demultiplexer_1_out18, demultiplexer_1_out19,
       demultiplexer_1_out20, demultiplexer_1_out21, demultiplexer_1_out22, demultiplexer_1_out23,
       demultiplexer_1_out24, demultiplexer_1_out25, demultiplexer_1_out26, demultiplexer_1_out27,
       demultiplexer_1_out28, demultiplexer_1_out29, demultiplexer_1_out30, demultiplexer_1_out31;

  Demultiplexer #(.select(5), .width(32), .enable("false")) demultiplexer_1 (
    .out0(demultiplexer_1_out0), .out1(demultiplexer_1_out1), .out2(demultiplexer_1_out2),
    .out3(demultiplexer_1_out3), .out4(demultiplexer_1_out4), .out5(demultiplexer_1_out5),
    .out6(demultiplexer_1_out6), .out7(demultiplexer_1_out7), .out8(demultiplexer_1_out8),
    .out9(demultiplexer_1_out9), .out10(demultiplexer_1_out10), .out11(demultiplexer_1_out11),
    .out12(demultiplexer_1_out12), .out13(demultiplexer_1_out13), .out14(demultiplexer_1_out14),
    .out15(demultiplexer_1_out15), .out16(demultiplexer_1_out16), .out17(demultiplexer_1_out17),
    .out18(demultiplexer_1_out18), .out19(demultiplexer_1_out19), .out20(demultiplexer_1_out20),
    .out21(demultiplexer_1_out21), .out22(demultiplexer_1_out22), .out23(demultiplexer_1_out23),
    .out24(demultiplexer_1_out24), .out25(demultiplexer_1_out25), .out26(demultiplexer_1_out26),
    .out27(demultiplexer_1_out27), .out28(demultiplexer_1_out28), .out29(demultiplexer_1_out29),
    .out30(demultiplexer_1_out30), .out31(demultiplexer_1_out31), .in(in_1), .sel(in_2));
  Demultiplexer #(.select(5), .enable("false")) demultiplexer_2 (
    .out0(demultiplexer_2_out0), .out1(demultiplexer_2_out1), .out2(demultiplexer_2_out2),
    .out3(demultiplexer_2_out3), .out4(demultiplexer_2_out4), .out5(demultiplexer_2_out5),
    .out6(demultiplexer_2_out6), .out7(demultiplexer_2_out7), .out8(demultiplexer_2_out8),
    .out9(demultiplexer_2_out9), .out10(demultiplexer_2_out10), .out11(demultiplexer_2_out11),
    .out12(demultiplexer_2_out12), .out13(demultiplexer_2_out13), .out14(demultiplexer_2_out14),
    .out15(demultiplexer_2_out15), .out16(demultiplexer_2_out16), .out17(demultiplexer_2_out17),
    .out18(demultiplexer_2_out18), .out19(demultiplexer_2_out19), .out20(demultiplexer_2_out20),
    .out21(demultiplexer_2_out21), .out22(demultiplexer_2_out22), .out23(demultiplexer_2_out23),
    .out24(demultiplexer_2_out24), .out25(demultiplexer_2_out25), .out26(demultiplexer_2_out26),
    .out27(demultiplexer_2_out27), .out28(demultiplexer_2_out28), .out29(demultiplexer_2_out29),
    .out30(demultiplexer_2_out30), .out31(demultiplexer_2_out31), .in(in_3), .sel(in_2));
  Register_part #(.width(32)) register_1 (
    .D(demultiplexer_1_out0), .en(demultiplexer_2_out0), .Q(out_6), .clk(in_4), .clr(in_5));
  Register_part #(.width(32)) register_2 (
    .D(demultiplexer_1_out1), .en(demultiplexer_2_out1), .Q(out_7), .clk(in_4), .clr(in_5));
  Register_part #(.width(32)) register_3 (
    .D(demultiplexer_1_out2), .en(demultiplexer_2_out2), .Q(out_8), .clk(in_4), .clr(in_5));
  Register_part #(.width(32)) register_4 (
    .D(demultiplexer_1_out3), .en(demultiplexer_2_out3), .Q(out_9), .clk(in_4), .clr(in_5));
  Register_part #(.width(32)) register_5 (
    .D(demultiplexer_1_out4), .en(demultiplexer_2_out4), .Q(out_10), .clk(in_4), .clr(in_5));
  Register_part #(.width(32)) register_6 (
    .D(demultiplexer_1_out5), .en(demultiplexer_2_out5), .Q(out_11), .clk(in_4), .clr(in_5));
  Register_part #(.width(32)) register_7 (
    .D(demultiplexer_1_out6), .en(demultiplexer_2_out6), .Q(out_12), .clk(in_4), .clr(in_5));
  Register_part #(.width(32)) register_8 (
    .D(demultiplexer_1_out7), .en(demultiplexer_2_out7), .Q(out_13), .clk(in_4), .clr(in_5));
  Register_part #(.width(32)) register_9 (
    .D(demultiplexer_1_out8), .en(demultiplexer_2_out8), .Q(out_14), .clk(in_4), .clr(in_5));
  Register_part #(.width(32)) register_10 (
    .D(demultiplexer_1_out9), .en(demultiplexer_2_out9), .Q(out_15), .clk(in_4), .clr(in_5));
  Register_part #(.width(32)) register_11 (
    .D(demultiplexer_1_out10), .en(demultiplexer_2_out10), .Q(out_16), .clk(in_4), .clr(in_5));
  Register_part #(.width(32)) register_12 (
    .D(demultiplexer_1_out11), .en(demultiplexer_2_out11), .Q(out_17), .clk(in_4), .clr(in_5));
  Register_part #(.width(32)) register_13 (
    .D(demultiplexer_1_out12), .en(demultiplexer_2_out12), .Q(out_18), .clk(in_4), .clr(in_5));
  Register_part #(.width(32)) register_14 (
    .D(demultiplexer_1_out13), .en(demultiplexer_2_out13), .Q(out_19), .clk(in_4), .clr(in_5));
  Register_part #(.width(32)) register_15 (
    .D(demultiplexer_1_out14), .en(demultiplexer_2_out14), .Q(out_20), .clk(in_4), .clr(in_5));
  Register_part #(.width(32)) register_16 (
    .D(demultiplexer_1_out15), .en(demultiplexer_2_out15), .Q(out_21), .clk(in_4), .clr(in_5));
  Register_part #(.width(32)) register_17 (
    .D(demultiplexer_1_out16), .en(demultiplexer_2_out16), .Q(out_22), .clk(in_4), .clr(in_5));
  Register_part #(.width(32)) register_18 (
    .D(demultiplexer_1_out17), .en(demultiplexer_2_out17), .Q(out_23), .clk(in_4), .clr(in_5));
  Register_part #(.width(32)) register_19 (
    .D(demultiplexer_1_out18), .en(demultiplexer_2_out18), .Q(out_24), .clk(in_4), .clr(in_5));
  Register_part #(.width(32)) register_20 (
    .D(demultiplexer_1_out19), .en(demultiplexer_2_out19), .Q(out_25), .clk(in_4), .clr(in_5));
  Register_part #(.width(32)) register_21 (
    .D(demultiplexer_1_out20), .en(demultiplexer_2_out20), .Q(out_26), .clk(in_4), .clr(in_5));
  Register_part #(.width(32)) register_22 (
    .D(demultiplexer_1_out21), .en(demultiplexer_2_out21), .Q(out_27), .clk(in_4), .clr(in_5));
  Register_part #(.width(32)) register_23 (
    .D(demultiplexer_1_out22), .en(demultiplexer_2_out22), .Q(out_28), .clk(in_4), .clr(in_5));
  Register_part #(.width(32)) register_24 (
    .D(demultiplexer_1_out23), .en(demultiplexer_2_out23), .Q(out_29), .clk(in_4), .clr(in_5));
  Register_part #(.width(32)) register_25 (
    .D(demultiplexer_1_out24), .en(demultiplexer_2_out24), .Q(out_30), .clk(in_4), .clr(in_5));
  Register_part #(.width(32)) register_26 (
    .D(demultiplexer_1_out25), .en(demultiplexer_2_out25), .Q(out_31), .clk(in_4), .clr(in_5));
  Register_part #(.width(32)) register_27 (
    .D(demultiplexer_1_out26), .en(demultiplexer_2_out26), .Q(out_32), .clk(in_4), .clr(in_5));
  Register_part #(.width(32)) register_28 (
    .D(demultiplexer_1_out27), .en(demultiplexer_2_out27), .Q(out_33), .clk(in_4), .clr(in_5));
  Register_part #(.width(32)) register_29 (
    .D(demultiplexer_1_out28), .en(demultiplexer_2_out28), .Q(out_34), .clk(in_4), .clr(in_5));
  Register_part #(.width(32)) register_30 (
    .D(demultiplexer_1_out29), .en(demultiplexer_2_out29), .Q(out_35), .clk(in_4), .clr(in_5));
  Register_part #(.width(32)) register_31 (
    .D(demultiplexer_1_out30), .en(demultiplexer_2_out30), .Q(out_36), .clk(in_4), .clr(in_5));
  Register_part #(.width(32)) register_32 (
    .D(demultiplexer_1_out31), .en(demultiplexer_2_out31), .Q(out_37), .clk(in_4), .clr(in_5));
endmodule

module RAL (
  input  in_1,
  input  [16:0] in_2,
  input  in_3,
  input  in_4,
  input  in_5,
  input  in_6,
  input  in_7,
  output [16:0] out_8
);

  wire and_1_out, j_k_ff_1_qn, j_k_ff_2_qn, j_k_ff_3_qn, j_k_ff_4_qn, j_k_ff_5_qn, j_k_ff_6_qn, j_k_ff_7_qn,
       j_k_ff_8_qn, j_k_ff_9_qn, j_k_ff_10_qn, j_k_ff_11_qn, j_k_ff_12_qn, j_k_ff_13_qn, j_k_ff_14_qn,
       j_k_ff_15_qn, j_k_ff_16_qn, j_k_ff_17_qn, or_1_out, or_2_out, or_3_out, or_4_out, or_5_out, or_6_out,
       or_7_out, or_8_out, or_9_out, or_10_out, or_11_out, or_12_out, or_13_out, or_14_out, or_15_out,
       or_16_out, or_17_out;
  wire [16:0] and_2_out, j_k_ff_17_q, rar_1_out_5;

  and and_1 (and_1_out, in_3, in_4);
  or or_1 (or_1_out, and_2_out[16], j_k_ff_17_q[0]);
  J_K_Flip_Flop j_k_ff_1 (
    .J(or_1_out), .clk(and_1_out), .K(j_k_ff_17_qn), .Q(j_k_ff_17_q[16]), .Qn(j_k_ff_1_qn), .reset(in_5));  // open: preset, en
  or or_2 (or_2_out, and_2_out[15], j_k_ff_17_q[16]);
  RAR rar_1 (.in_1(in_1), .in_2(and_2_out), .in_3(and_1_out), .in_4(in_5), .out_5(rar_1_out_5));
  J_K_Flip_Flop j_k_ff_2 (
    .J(or_2_out), .clk(and_1_out), .K(j_k_ff_1_qn), .Q(j_k_ff_17_q[15]), .Qn(j_k_ff_2_qn), .reset(in_5));  // open: preset, en
  assign out_8 = in_7 ? rar_1_out_5 : 17'bz;  // Controlled_Buffer controlled_buffer_1
  assign and_2_out = {17{in_1}} & in_2;  // AND_Gate and_2, 17 bits wide
  or or_3 (or_3_out, and_2_out[14], j_k_ff_17_q[15]);
  J_K_Flip_Flop j_k_ff_3 (
    .J(or_3_out), .clk(and_1_out), .K(j_k_ff_2_qn), .Q(j_k_ff_17_q[14]), .Qn(j_k_ff_3_qn), .reset(in_5));  // open: preset, en
  or or_4 (or_4_out, and_2_out[13], j_k_ff_17_q[14]);
  J_K_Flip_Flop j_k_ff_4 (
    .J(or_4_out), .clk(and_1_out), .K(j_k_ff_3_qn), .Q(j_k_ff_17_q[13]), .Qn(j_k_ff_4_qn), .reset(in_5));  // open: preset, en
  or or_5 (or_5_out, and_2_out[12], j_k_ff_17_q[13]);
  J_K_Flip_Flop j_k_ff_5 (
    .J(or_5_out), .clk(and_1_out), .K(j_k_ff_4_qn), .Q(j_k_ff_17_q[12]), .Qn(j_k_ff_5_qn), .reset(in_5));  // open: preset, en
  or or_6 (or_6_out, and_2_out[11], j_k_ff_17_q[12]);
  J_K_Flip_Flop j_k_ff_6 (
    .J(or_6_out), .clk(and_1_out), .K(j_k_ff_5_qn), .Q(j_k_ff_17_q[11]), .Qn(j_k_ff_6_qn), .reset(in_5));  // open: preset, en
  or or_7 (or_7_out, and_2_out[10], j_k_ff_17_q[11]);
  J_K_Flip_Flop j_k_ff_7 (
    .J(or_7_out), .clk(and_1_out), .K(j_k_ff_6_qn), .Q(j_k_ff_17_q[10]), .Qn(j_k_ff_7_qn), .reset(in_5));  // open: preset, en
  or or_8 (or_8_out, and_2_out[9], j_k_ff_17_q[10]);
  J_K_Flip_Flop j_k_ff_8 (
    .J(or_8_out), .clk(and_1_out), .K(j_k_ff_7_qn), .Q(j_k_ff_17_q[9]), .Qn(j_k_ff_8_qn), .reset(in_5));  // open: preset, en
  or or_9 (or_9_out, and_2_out[8], j_k_ff_17_q[9]);
  assign out_8 = in_6 ? j_k_ff_17_q : 17'bz;  // Controlled_Buffer controlled_buffer_2
  J_K_Flip_Flop j_k_ff_9 (
    .J(or_9_out), .clk(and_1_out), .K(j_k_ff_8_qn), .Q(j_k_ff_17_q[8]), .Qn(j_k_ff_9_qn), .reset(in_5));  // open: preset, en
  or or_10 (or_10_out, and_2_out[7], j_k_ff_17_q[8]);
  J_K_Flip_Flop j_k_ff_10 (
    .J(or_10_out), .clk(and_1_out), .K(j_k_ff_9_qn), .Q(j_k_ff_17_q[7]), .Qn(j_k_ff_10_qn), .reset(in_5));  // open: preset, en
  or or_11 (or_11_out, and_2_out[6], j_k_ff_17_q[7]);
  J_K_Flip_Flop j_k_ff_11 (
    .J(or_11_out), .clk(and_1_out), .K(j_k_ff_10_qn), .Q(j_k_ff_17_q[6]), .Qn(j_k_ff_11_qn), .reset(in_5));  // open: preset, en
  J_K_Flip_Flop j_k_ff_12 (
    .J(or_12_out), .clk(and_1_out), .K(j_k_ff_11_qn), .Q(j_k_ff_17_q[5]), .Qn(j_k_ff_12_qn), .reset(in_5));  // open: preset, en
  or or_12 (or_12_out, and_2_out[5], j_k_ff_17_q[6]);
  or or_13 (or_13_out, and_2_out[4], j_k_ff_17_q[5]);
  J_K_Flip_Flop j_k_ff_13 (
    .J(or_13_out), .clk(and_1_out), .K(j_k_ff_12_qn), .Q(j_k_ff_17_q[4]), .Qn(j_k_ff_13_qn), .reset(in_5));  // open: preset, en
  or or_14 (or_14_out, and_2_out[3], j_k_ff_17_q[4]);
  J_K_Flip_Flop j_k_ff_14 (
    .J(or_14_out), .clk(and_1_out), .K(j_k_ff_13_qn), .Q(j_k_ff_17_q[3]), .Qn(j_k_ff_14_qn), .reset(in_5));  // open: preset, en
  or or_15 (or_15_out, and_2_out[2], j_k_ff_17_q[3]);
  J_K_Flip_Flop j_k_ff_15 (
    .J(or_15_out), .clk(and_1_out), .K(j_k_ff_14_qn), .Q(j_k_ff_17_q[2]), .Qn(j_k_ff_15_qn), .reset(in_5));  // open: preset, en
  or or_16 (or_16_out, and_2_out[1], j_k_ff_17_q[2]);
  J_K_Flip_Flop j_k_ff_16 (
    .J(or_16_out), .clk(and_1_out), .K(j_k_ff_15_qn), .Q(j_k_ff_17_q[1]), .Qn(j_k_ff_16_qn), .reset(in_5));  // open: preset, en
  or or_17 (or_17_out, and_2_out[0], j_k_ff_17_q[1]);
  J_K_Flip_Flop j_k_ff_17 (
    .J(or_17_out), .clk(and_1_out), .K(j_k_ff_16_qn), .Q(j_k_ff_17_q[0]), .Qn(j_k_ff_17_qn), .reset(in_5));  // open: preset, en
endmodule

module RAR (
  input  in_1,
  input  [16:0] in_2,
  input  in_3,
  input  in_4,
  output [16:0] out_5
);

  wire j_k_ff_1_qn, j_k_ff_2_qn, j_k_ff_3_qn, j_k_ff_4_qn, j_k_ff_5_qn, j_k_ff_6_qn, j_k_ff_7_qn,
       j_k_ff_8_qn, j_k_ff_9_qn, j_k_ff_10_qn, j_k_ff_11_qn, j_k_ff_12_qn, j_k_ff_13_qn, j_k_ff_14_qn,
       j_k_ff_15_qn, j_k_ff_16_qn, j_k_ff_17_qn, or_1_out, or_2_out, or_3_out, or_4_out, or_5_out, or_6_out,
       or_7_out, or_8_out, or_9_out, or_10_out, or_11_out, or_12_out, or_13_out, or_14_out, or_15_out,
       or_16_out, or_17_out;
  wire [16:0] and_1_out;

  or or_1 (or_1_out, out_5[15], and_1_out[16]);
  J_K_Flip_Flop j_k_ff_1 (
    .J(or_1_out), .clk(in_3), .K(j_k_ff_2_qn), .Q(out_5[16]), .Qn(j_k_ff_1_qn), .reset(in_4));  // open: preset, en
  or or_2 (or_2_out, out_5[14], and_1_out[15]);
  J_K_Flip_Flop j_k_ff_2 (
    .J(or_2_out), .clk(in_3), .K(j_k_ff_3_qn), .Q(out_5[15]), .Qn(j_k_ff_2_qn), .reset(in_4));  // open: preset, en
  or or_3 (or_3_out, out_5[13], and_1_out[14]);
  J_K_Flip_Flop j_k_ff_3 (
    .J(or_3_out), .clk(in_3), .K(j_k_ff_4_qn), .Q(out_5[14]), .Qn(j_k_ff_3_qn), .reset(in_4));  // open: preset, en
  assign and_1_out = {17{in_1}} & in_2;  // AND_Gate and_1, 17 bits wide
  or or_4 (or_4_out, out_5[12], and_1_out[13]);
  J_K_Flip_Flop j_k_ff_4 (
    .J(or_4_out), .clk(in_3), .K(j_k_ff_5_qn), .Q(out_5[13]), .Qn(j_k_ff_4_qn), .reset(in_4));  // open: preset, en
  or or_5 (or_5_out, out_5[11], and_1_out[12]);
  J_K_Flip_Flop j_k_ff_5 (
    .J(or_5_out), .clk(in_3), .K(j_k_ff_6_qn), .Q(out_5[12]), .Qn(j_k_ff_5_qn), .reset(in_4));  // open: preset, en
  or or_6 (or_6_out, out_5[10], and_1_out[11]);
  J_K_Flip_Flop j_k_ff_6 (
    .J(or_6_out), .clk(in_3), .K(j_k_ff_7_qn), .Q(out_5[11]), .Qn(j_k_ff_6_qn), .reset(in_4));  // open: preset, en
  or or_7 (or_7_out, out_5[9], and_1_out[10]);
  J_K_Flip_Flop j_k_ff_7 (
    .J(or_7_out), .clk(in_3), .K(j_k_ff_8_qn), .Q(out_5[10]), .Qn(j_k_ff_7_qn), .reset(in_4));  // open: preset, en
  or or_8 (or_8_out, out_5[8], and_1_out[9]);
  J_K_Flip_Flop j_k_ff_8 (
    .J(or_8_out), .clk(in_3), .K(j_k_ff_9_qn), .Q(out_5[9]), .Qn(j_k_ff_8_qn), .reset(in_4));  // open: preset, en
  J_K_Flip_Flop j_k_ff_9 (
    .J(or_9_out), .clk(in_3), .K(j_k_ff_10_qn), .Q(out_5[8]), .Qn(j_k_ff_9_qn), .reset(in_4));  // open: preset, en
  or or_9 (or_9_out, out_5[7], and_1_out[8]);
  or or_10 (or_10_out, out_5[6], and_1_out[7]);
  J_K_Flip_Flop j_k_ff_10 (
    .J(or_10_out), .clk(in_3), .K(j_k_ff_11_qn), .Q(out_5[7]), .Qn(j_k_ff_10_qn), .reset(in_4));  // open: preset, en
  J_K_Flip_Flop j_k_ff_11 (
    .J(or_11_out), .clk(in_3), .K(j_k_ff_12_qn), .Q(out_5[6]), .Qn(j_k_ff_11_qn), .reset(in_4));  // open: preset, en
  or or_11 (or_11_out, out_5[5], and_1_out[6]);
  or or_12 (or_12_out, out_5[4], and_1_out[5]);
  J_K_Flip_Flop j_k_ff_12 (
    .J(or_12_out), .clk(in_3), .K(j_k_ff_13_qn), .Q(out_5[5]), .Qn(j_k_ff_12_qn), .reset(in_4));  // open: preset, en
  or or_13 (or_13_out, out_5[3], and_1_out[4]);
  J_K_Flip_Flop j_k_ff_13 (
    .J(or_13_out), .clk(in_3), .K(j_k_ff_14_qn), .Q(out_5[4]), .Qn(j_k_ff_13_qn), .reset(in_4));  // open: preset, en
  or or_14 (or_14_out, out_5[2], and_1_out[3]);
  J_K_Flip_Flop j_k_ff_14 (
    .J(or_14_out), .clk(in_3), .K(j_k_ff_15_qn), .Q(out_5[3]), .Qn(j_k_ff_14_qn), .reset(in_4));  // open: preset, en
  or or_15 (or_15_out, out_5[1], and_1_out[2]);
  J_K_Flip_Flop j_k_ff_15 (
    .J(or_15_out), .clk(in_3), .K(j_k_ff_16_qn), .Q(out_5[2]), .Qn(j_k_ff_15_qn), .reset(in_4));  // open: preset, en
  or or_16 (or_16_out, out_5[0], and_1_out[1]);
  J_K_Flip_Flop j_k_ff_16 (
    .J(or_16_out), .clk(in_3), .K(j_k_ff_17_qn), .Q(out_5[1]), .Qn(j_k_ff_16_qn), .reset(in_4));  // open: preset, en
  or or_17 (or_17_out, out_5[16], and_1_out[0]);
  J_K_Flip_Flop j_k_ff_17 (
    .J(or_17_out), .clk(in_3), .K(j_k_ff_1_qn), .Q(out_5[0]), .Qn(j_k_ff_17_qn), .reset(in_4));  // open: preset, en
endmodule

module main (
  input  in_1,
  input  in_2,
  input  in_3,
  input  in_4,
  input  in_5,
  input  in_6,
  input  [15:0] in_7,
  input  [15:0] in_8
);

  wire CLK, CLR, IN2, OUT2, RD, WR;
  wire [4:0] bit_extender_1_out;
  wire [6:0] DATA, IN1;
  wire [15:0] a, b, c, cpu_1_ram_data_2, d, e, h, l, PC, STACK;
  wire [31:0] screendriver_1_out_6, screendriver_1_out_7, screendriver_1_out_8, screendriver_1_out_9,
       screendriver_1_out_10, screendriver_1_out_11, screendriver_1_out_12, screendriver_1_out_13,
       screendriver_1_out_14, screendriver_1_out_15, screendriver_1_out_16, screendriver_1_out_17,
       screendriver_1_out_18, screendriver_1_out_19, screendriver_1_out_20, screendriver_1_out_21,
       screendriver_1_out_22, screendriver_1_out_23, screendriver_1_out_24, screendriver_1_out_25,
       screendriver_1_out_26, screendriver_1_out_27, screendriver_1_out_28, screendriver_1_out_29,
       screendriver_1_out_30, screendriver_1_out_31, screendriver_1_out_32, screendriver_1_out_33,
       screendriver_1_out_34, screendriver_1_out_35, screendriver_1_out_36, screendriver_1_out_37;

  CPU cpu_1 (
    .EN_CLK(in_1), .STEP(in_2), .CLR(in_3), .in_8(in_4), .KEYBOARD_RD(RD), .IN_2(IN2), .IN_1(IN1), .WR_2(WR),
    .WR(DATA), .OUT2(OUT2), .A(a), .B(b), .C(c), .D(d), .E(e), .H(h), .L(l), .RAM_ADDRESS(in_7),
    .RAM_DATA(in_8), .LD(in_5), .EN(in_6), .RAM_DATA_2(cpu_1_ram_data_2), .CLR_OUT(CLR), .CLK_OUT(CLK),
    .pc(PC), .STACK(STACK));
  Hex_Digit_Display hex_digit_display_1 (.value(a[15:12]));  // open: dp
  Hex_Digit_Display hex_digit_display_2 (.value(a[11:8]));  // open: dp
  Hex_Digit_Display hex_digit_display_3 (.value(c[11:8]));  // open: dp
  Hex_Digit_Display hex_digit_display_4 (.value(c[15:12]));  // open: dp
  Hex_Digit_Display hex_digit_display_5 (.value(e[15:12]));  // open: dp
  Hex_Digit_Display hex_digit_display_6 (.value(e[11:8]));  // open: dp
  Hex_Digit_Display hex_digit_display_7 (.value(PC[15:12]));  // open: dp
  Hex_Digit_Display hex_digit_display_8 (.value(PC[11:8]));  // open: dp
  Hex_Digit_Display hex_digit_display_9 (.value(a[3:0]));  // open: dp
  Hex_Digit_Display hex_digit_display_10 (.value(a[7:4]));  // open: dp
  Hex_Digit_Display hex_digit_display_11 (.value(c[7:4]));  // open: dp
  Hex_Digit_Display hex_digit_display_12 (.value(c[3:0]));  // open: dp
  Hex_Digit_Display hex_digit_display_13 (.value(e[7:4]));  // open: dp
  Hex_Digit_Display hex_digit_display_14 (.value(e[3:0]));  // open: dp
  Hex_Digit_Display hex_digit_display_15 (.value(PC[3:0]));  // open: dp
  Hex_Digit_Display hex_digit_display_16 (.value(PC[7:4]));  // open: dp
  Hex_Digit_Display hex_digit_display_17 (.value(cpu_1_ram_data_2[15:12]));  // open: dp
  Hex_Digit_Display hex_digit_display_18 (.value(h[15:12]));  // open: dp
  Hex_Digit_Display hex_digit_display_19 (.value(cpu_1_ram_data_2[7:4]));  // open: dp
  Hex_Digit_Display hex_digit_display_20 (.value(cpu_1_ram_data_2[11:8]));  // open: dp
  Hex_Digit_Display hex_digit_display_21 (.value(b[15:12]));  // open: dp
  Hex_Digit_Display hex_digit_display_22 (.value(d[15:12]));  // open: dp
  Hex_Digit_Display hex_digit_display_23 (.value(h[7:4]));  // open: dp
  Hex_Digit_Display hex_digit_display_24 (.value(h[11:8]));  // open: dp
  Hex_Digit_Display hex_digit_display_25 (.value(STACK[11:8]));  // open: dp
  Hex_Digit_Display hex_digit_display_26 (.value(STACK[15:12]));  // open: dp
  Hex_Digit_Display hex_digit_display_27 (.value(cpu_1_ram_data_2[3:0]));  // open: dp
  Hex_Digit_Display hex_digit_display_28 (.value(b[11:8]));  // open: dp
  Hex_Digit_Display hex_digit_display_29 (.value(b[7:4]));  // open: dp
  Hex_Digit_Display hex_digit_display_30 (.value(d[7:4]));  // open: dp
  Hex_Digit_Display hex_digit_display_31 (.value(d[11:8]));  // open: dp
  Hex_Digit_Display hex_digit_display_32 (.value(h[3:0]));  // open: dp
  Hex_Digit_Display hex_digit_display_33 (.value(l[15:12]));  // open: dp
  Hex_Digit_Display hex_digit_display_34 (.value(STACK[7:4]));  // open: dp
  Hex_Digit_Display hex_digit_display_35 (.value(STACK[3:0]));  // open: dp
  Hex_Digit_Display hex_digit_display_36 (.value(b[3:0]));  // open: dp
  Hex_Digit_Display hex_digit_display_37 (.value(d[3:0]));  // open: dp
  Hex_Digit_Display hex_digit_display_38 (.value(l[11:8]));  // open: dp
  Hex_Digit_Display hex_digit_display_39 (.value(l[7:4]));  // open: dp
  DotMatrix #(.inputtype("row"), .matrixcols(32), .matrixrows(32)) dotmatrix_1 (
    .row0(screendriver_1_out_6), .row1(screendriver_1_out_7), .row2(screendriver_1_out_8),
    .row3(screendriver_1_out_9), .row4(screendriver_1_out_10), .row5(screendriver_1_out_11),
    .row6(screendriver_1_out_12), .row7(screendriver_1_out_13), .row8(screendriver_1_out_14),
    .row9(screendriver_1_out_15), .row10(screendriver_1_out_16), .row11(screendriver_1_out_17),
    .row12(screendriver_1_out_18), .row13(screendriver_1_out_19), .row14(screendriver_1_out_20),
    .row15(screendriver_1_out_21), .row16(screendriver_1_out_22), .row17(screendriver_1_out_23),
    .row18(screendriver_1_out_24), .row19(screendriver_1_out_25), .row20(screendriver_1_out_26),
    .row21(screendriver_1_out_27), .row22(screendriver_1_out_28), .row23(screendriver_1_out_29),
    .row24(screendriver_1_out_30), .row25(screendriver_1_out_31), .row26(screendriver_1_out_32),
    .row27(screendriver_1_out_33), .row28(screendriver_1_out_34), .row29(screendriver_1_out_35),
    .row30(screendriver_1_out_36), .row31(screendriver_1_out_37));
  ScreenDriver screendriver_1 (
    .in_1({d, e}), .in_2(bit_extender_1_out), .in_3(OUT2), .out_6(screendriver_1_out_6),
    .out_7(screendriver_1_out_7), .out_8(screendriver_1_out_8), .out_9(screendriver_1_out_9),
    .out_10(screendriver_1_out_10), .out_11(screendriver_1_out_11), .out_12(screendriver_1_out_12),
    .out_13(screendriver_1_out_13), .out_14(screendriver_1_out_14), .out_15(screendriver_1_out_15),
    .out_16(screendriver_1_out_16), .out_17(screendriver_1_out_17), .out_18(screendriver_1_out_18),
    .out_19(screendriver_1_out_19), .out_20(screendriver_1_out_20), .out_21(screendriver_1_out_21),
    .out_22(screendriver_1_out_22), .out_23(screendriver_1_out_23), .out_24(screendriver_1_out_24),
    .out_25(screendriver_1_out_25), .out_26(screendriver_1_out_26), .out_27(screendriver_1_out_27),
    .out_28(screendriver_1_out_28), .out_29(screendriver_1_out_29), .out_30(screendriver_1_out_30),
    .out_31(screendriver_1_out_31), .out_32(screendriver_1_out_32), .out_33(screendriver_1_out_33),
    .out_34(screendriver_1_out_34), .out_35(screendriver_1_out_35), .out_36(screendriver_1_out_36),
    .out_37(screendriver_1_out_37), .in_5(CLR), .in_4(CLK));
  Bit_Extender #(.in_width(16), .out_width(5)) bit_extender_1 (.in(c), .out(bit_extender_1_out));
  TTY tty_1 (.data(DATA), .clk(CLK), .we(WR), .clr(CLR));
  Hex_Digit_Display hex_digit_display_40 (.value(l[3:0]));  // open: dp
  Keyboard keyboard_1 (.clk(CLK), .re(RD), .clr(CLR), .avail(IN2), .data(IN1));

  // Notes on the sheet:
  //   06 - MOV A,A 
  //   08 - MOV A,B
  //   0a - MOV A,C
  //   0c - MOV A,D
  //   0e - MOV A,E
  //   10 - MOV A,H
  //   12 - MOV A,L
  //   6c - MOV H,A
  //   6e - MOV H,B
  //   05 -HULT
  //   da - STC
  //   f3 - ADD M(L REG)
  //   14 - MOV A, M(L REG)
  //   28 - MOV C,A
  //   2a - MOV C,B
  //   2c - MOV C,C
  //   2e - MOV C,D
  //   30 - MOV C,E
  //   32 - MOV C,L
  //   34 - MOV C,H
  //   36 - MOV C,M(L REG)
  //   4a - MOV E,A
  //   4c - MOV E,B
  //   4e - MOV E,C
  //   50 - MOV E,D
  //   52 - MOV E,E
  //   54 - MOV E,L
  //   56 - MOV E,H
  //   58 - MOV E,M(L REG)
  //   70 - MOV H,C
  //   72 - MOV H,D
  //   74 - MOV H,E
  //   76 - MOV H,L
  //   78 - MOV H,H 
  //   7a - MOV H,M(L REG)
  //   92 - MVI A,dd
  //   95 - MVi B,dd
  //   98 - MVi C,dd
  //   301 - MVI D,dd
  //   9e - MVI E,dd
  //   a1 - MVI Hdd
  //   a4 - MVI L,dd
  //   03 - NOP
  //   dc - CMC
  //   de - ADD A
  //   e1 - ADD B
  //   e4 - ADD C
  //   e7 - ADD D
  //   ea - ADD E
  //   ed - ADD H
  //   f0 - ADD L
  //   118 - SUB A
  //   11b - SUB B
  //   11e - SUB C
  //   121 - SUB D
  //   124 - SUB E
  //   127 - SUB H
  //   12a - SUB L
  //   12d - SUB M(L REG)
  //   152 - DAD B
  //   159 - DAD D
  //   160 - DAD H
  //   167 - ADI dd
  //   16b - ACI dd
  //   170 - SUI dd
  //   174 - SBI dd
  //   179 - DAA 
  //   194 - XRA A
  //   197 - XRA B
  //   19a - XRA C
  //   19d - XRA D
  //   1a0 - XRA E
  //   1a3 - XRA H
  //   1a6 - XRA L
  //   1a9 - XRA M(L REG)
  //   FIX->
  //   17 - MOV B,A
  //   19 - MOV B,B
  //   1b - MOV B,C
  //   1d - MOV B,D
  //   1f - MOV B,E
  //   21 - MOV B,L
  //   23 - MOV B,H 
  //   25 - MOV B, M(L REG)
  //   39 - MOV D,A
  //   3b - MOV D,B
  //   3d - MOV D,C
  //   3f - MOV D,D
  //   41 - MOV D,E
  //   43 - MOV D,L
  //   45 - MOV D,H
  //   47 - MOV C, M(L REG)
  //   5b -MOV L,A
  //   5d - MOV L,B
  //   5f - MOV L,C
  //   61 - MOV L,D
  //   63 - MOV L,E
  //   65 - MOV L,H
  //   67 - MOV L,L
  //   69 - MOV L,M (L REG) 
  //   7d - MOV - M(L REG), A
  //   80 - MOV - M(L REG), B
  //   83 - MOV -M,(L REG),C
  //   86 - MOV - M,(L REG), D
  //   89 - MOV - M,(L REG) E
  //   8c - MOV - M(L REG), L
  //   8f - MOV - M(L REG),H
  //   a7 - LXI B,dddd
  //   ac - LXI D,dddd
  //   b1 - LXI H,dddd
  //   b6 - LDAX B
  //   b9 - LDAX D
  //   bc - LHLD aaaa
  //   c3 - LDA  aa
  //   c6 - STA aa
  //   cb - ATAX B
  //   c7 - ATAX D
  //   ce - SHLD aaaa
  //   d3 - XCHG
  //   f7 - ADC A
  //   fb - ADC B
  //   ff - ADC C
  //   103 - ADC D
  //   107 - ADC E
  //   10b - ADC H
  //   10f - ADC L
  //   113 - ADC M(L REG)
  //   131 - SBB A
  //   135 -  SBB B
  //   139 - SBB C
  //   13d - SBB D
  //   141 -  SBB E
  //   145 - SBB H
  //   149 - SBB L
  //   14d - SBB M(L REG)
  //   17b - AND A
  //   17e - AND B
  //   181 - AND C
  //   184 - AND D
  //   187 - AND E
  //   18a - AND H
  //   18d - AND L
  //   190 - AND M(L REG)
  //   1ad - ORA A
  //   1b0 - ORA B
  //   1b3 - ORA C
  //   1b6 - ORA D
  //   1b9 - ORA E
  //   1bc - ORA H
  //   1bf - ORA L
  //   1c2 - ORA M(L REG)
  //   1c6 - ANI dd
  //   1ca - XRI dd
  //   1ce - ORI dd
  //   1d2 - CMA
  //   1d4 - RLC
  //   1d8 - RRC
  //   1dc - RAR
  //   1de - RAL
  //   1e0 - INR A
  //   1e2 - INR B
  //   1e4 - INR C
  //   1e6 - INR D
  //   1e8 - INR E
  //   1ea - INR H
  //   1ec - INR L
  //   1fc - INR M(L REG)
  //   1ee - DCR A
  //   1f0 - DCR B
  //   1f2 - DCR C
  //   1f4 - DCR D
  //   1f6 - DCR E
  //   1f8- DCR H
  //   1fa - DCR L
  //   201 - DCR M(L REG)
  //   206 - INX B
  //   209 - INX D
  //   20c - INX H
  //   20f - DCX B
  //   212  - DCX D
  //   215 - DCX H
  //   218 - JMP aaaa
  //   21a - PCHL
  //   21d - CMP A
  //   220 - CMP B
  //   223 - CMP C
  //   226 - CMP D
  //   229 - CMP E
  //   22c - CMP H
  //   22f - CMP L
  //   232 - CMP M(L REG)
  //   236 - CPI dd
  //   23d - JNZ aaaa
  //   23a - JZ aaaa
  //   240 - JNC aaaa
  //   243 - JC aaaa
  //   246 - JPO aaaa
  //   249 - JPE aaaa
  //   24c - JP aaaa
  //   24f - JM aaaa
  //   252 - CALL aaaa
  //   258 - CNZ aaaa
  //   25f - CZ aaaa
  //   266 - CC aaaa
  //   26d - CNC aaaa
  //   274 - CPE aaaa
  //   27b - CPO aaaa
  //   282 - CP aaaa
  //   281 - CM aaaa
  //   290 - RET
  //   293 - RNZ
  //   297 - RZ
  //   29b - RC
  //   29f - RNC
  //   2a3 - RPE
  //   2a7 - RPO
  //   2ab - RP
  //   2af - RM
  //   2b3 - LXI SP,dddd
  //   2b6 - DAD SP
  //   2b9 - INX SP
  //   2bb - DCX SP
  //   2bd - PUSH B
  //   2c4 - PUSH D
  //   2cb - PUSH H
  //   2d3 - PUSH PSW
  //   2da - POP B
  //   2df - POP D
  //   2e4 - POP H
  //   2e9 - POP PSW
  //   2ee - XTHL
  //   2f7 - SPHL
  //   2f9 - IN 1
  //   2fb - IN 2
  //   2fd - OUT 1
  //   2ff - OUT 2
endmodule
